// Logisim project 8bitcomp.circ as structural Verilog
module main (
);

  wire alu_1_cf, alu_1_s0, alu_1_s1, alu_1_s2, alu_1_s3, alu_1_s4, alu_1_s5, alu_1_s6, alu_1_s7, alu_1_zf,
       and_1_out, bit_to_7segment_1_a1, bit_to_7segment_1_a2, bit_to_7segment_1_a3, bit_to_7segment_1_b1,
       bit_to_7segment_1_b2, bit_to_7segment_1_b3, bit_to_7segment_1_c1, bit_to_7segment_1_c2,
       bit_to_7segment_1_c3, bit_to_7segment_1_d1, bit_to_7segment_1_d2, bit_to_7segment_1_d3,
       bit_to_7segment_1_e1, bit_to_7segment_1_e2, bit_to_7segment_1_e3, bit_to_7segment_1_f1,
       bit_to_7segment_1_f2, bit_to_7segment_1_f3, bit_to_7segment_1_g1, bit_to_7segment_1_g2,
       bit_to_7segment_1_g3, bitregister_1_o0, bitregister_1_o1, bitregister_1_o2, bitregister_1_o3,
       bitregister_1_o4, bitregister_1_o5, bitregister_1_o6, bitregister_1_o7, bitregister_2_o0,
       bitregister_2_o1, bitregister_2_o2, bitregister_2_o3, bitregister_2_o4, bitregister_2_o5,
       bitregister_2_o6, bitregister_2_o7, bitregister_3_o0, bitregister_3_o1, bitregister_3_o2,
       bitregister_3_o3, bitregister_3_o4, bitregister_3_o5, bitregister_3_o6, bitregister_3_o7,
       bitregister_4_o0, bitregister_4_o1, bitregister_4_o2, bitregister_4_o3, bitregister_4_o4,
       bitregister_4_o5, bitregister_4_o6, bitregister_4_o7, bitregister_5_o0, bitregister_5_o1,
       bitregister_5_o2, bitregister_5_o3, bitregister_5_o4, bitregister_5_o5, bitregister_5_o6,
       bitregister_5_o7, bitregister_6_o0, bitregister_6_o1, bitregister_6_o2, bitregister_6_o3,
       bitregister_6_o4, bitregister_6_o5, bitregister_6_o6, bitregister_6_o7, bitregister_7_o0,
       bitregister_7_o1, bitregister_7_o2, bitregister_7_o3, bitregister_7_o4, bitregister_7_o5,
       bitregister_7_o6, bitregister_7_o7, bitregister_8_o0, bitregister_8_o1, bitregister_8_o2,
       bitregister_8_o3, bitregister_8_o4, bitregister_8_o5, bitregister_8_o6, bitregister_8_o7,
       bitregister_9_o0, bitregister_9_o1, bitregister_9_o2, bitregister_9_o3, bitregister_9_o4,
       bitregister_9_o5, bitregister_9_o6, bitregister_9_o7, boot_strap_control_unit_1_bootstrapmode,
       boot_strap_control_unit_1_ram_wr, boot_strap_control_unit_1_reg_rd, clk_1_o,
       control_unit_vhardwired_1_a_rd_en, control_unit_vhardwired_1_a_wr_en,
       control_unit_vhardwired_1_b_rd_en, control_unit_vhardwired_1_b_wr_en,
       control_unit_vhardwired_1_c_rd_en, control_unit_vhardwired_1_c_wr_en,
       control_unit_vhardwired_1_d_rd_en, control_unit_vhardwired_1_d_wr_en, control_unit_vhardwired_1_halt,
       control_unit_vhardwired_1_ir, control_unit_vhardwired_1_mar_in, control_unit_vhardwired_1_pc_inc,
       control_unit_vhardwired_1_pc_out, control_unit_vhardwired_1_pc_wr, counter_8_bts_1_d0,
       counter_8_bts_1_d1, counter_8_bts_1_d2, counter_8_bts_1_d3, counter_8_bts_1_d4, counter_8_bts_1_d5,
       counter_8_bts_1_d6, counter_8_bts_1_d7, flagreg_1_cf, flagreg_1_zf, or_1_out, Reset_out,
       sram_256_bytes_1_s0, sram_256_bytes_1_s1, sram_256_bytes_1_s2, sram_256_bytes_1_s3,
       sram_256_bytes_1_s4, sram_256_bytes_1_s5, sram_256_bytes_1_s6, sram_256_bytes_1_s7,
       sram_256_bytes_2_s0, sram_256_bytes_2_s1, sram_256_bytes_2_s2, sram_256_bytes_2_s3,
       sram_256_bytes_2_s4, sram_256_bytes_2_s5, sram_256_bytes_2_s6, sram_256_bytes_2_s7, switch_1_p2;
  wire [3:0] bitregister_7_reg_out, bitregister_7_reg_out_2, bitregister_8_reg_out, bitregister_8_reg_out_2;
  wire [7:0] bitregister_1_reg_out, bitregister_4_reg_out, bitregister_6_reg_out, bitregister_9_reg_out,
       boot_strap_control_unit_1_o, boot_strap_control_unit_1_r_addr, multiplexer_1_out, rom_1_data;

  DotMatrix #(.dotshape("circle"), .inputtype("row"), .matrixcols(1), .matrixrows(8)) dotmatrix_1 (
    .row0(bitregister_1_o0), .row1(bitregister_1_o1), .row2(bitregister_1_o2), .row3(bitregister_1_o3),
    .row4(bitregister_1_o4), .row5(bitregister_1_o5), .row6(bitregister_1_o6), .row7(bitregister_1_o7));
  BitRegister bitregister_1 (
    .reset(Reset_out), .Load(control_unit_vhardwired_1_a_wr_en), .CLK(clk_1_o),
    .reg_in(bitregister_1_reg_out), .reg_out_en(control_unit_vhardwired_1_a_rd_en),
    .reg_out(bitregister_1_reg_out), .O5(bitregister_1_o5), .O6(bitregister_1_o6), .O7(bitregister_1_o7),
    .O0(bitregister_1_o0), .O1(bitregister_1_o1), .O2(bitregister_1_o2), .O3(bitregister_1_o3),
    .O4(bitregister_1_o4));
  Control_Unit_VHardwired control_unit_vhardwired_1 (
    .Enable(boot_strap_control_unit_1_bootstrapmode), .CLK(clk_1_o), .Reset(Reset_out),
    .I4(bitregister_1_reg_out[4]), .I5(bitregister_1_reg_out[5]), .I6(bitregister_1_reg_out[6]),
    .I7(bitregister_1_reg_out[7]), .I2(bitregister_1_reg_out[2]), .I3(bitregister_1_reg_out[3]),
    .I0(bitregister_1_reg_out[0]), .I1(bitregister_1_reg_out[1]), .PC_OUT(control_unit_vhardwired_1_pc_out),
    .MAR_IN(control_unit_vhardwired_1_mar_in), .IR(control_unit_vhardwired_1_ir),
    .PC_INC(control_unit_vhardwired_1_pc_inc), .Halt(control_unit_vhardwired_1_halt),
    .PC_WR(control_unit_vhardwired_1_pc_wr), .A_RD_EN(control_unit_vhardwired_1_a_rd_en),
    .B_RD_EN(control_unit_vhardwired_1_b_rd_en), .C_RD_EN(control_unit_vhardwired_1_c_rd_en),
    .D_RD_EN(control_unit_vhardwired_1_d_rd_en), .A_WR_EN(control_unit_vhardwired_1_a_wr_en),
    .B_WR_EN(control_unit_vhardwired_1_b_wr_en), .C_WR_EN(control_unit_vhardwired_1_c_wr_en),
    .D_WR_EN(control_unit_vhardwired_1_d_wr_en));  // open: REG_WR_B, T0, T1, T2, T3, T4, T5, T6, T7, S0, S1, S2, S3
  DotMatrix #(.dotshape("circle"), .inputtype("row"), .matrixcols(1), .matrixrows(8)) dotmatrix_2 (
    .row0(bitregister_2_o0), .row1(bitregister_2_o1), .row2(bitregister_2_o2), .row3(bitregister_2_o3),
    .row4(bitregister_2_o4), .row5(bitregister_2_o5), .row6(bitregister_2_o6), .row7(bitregister_2_o7));
  BitRegister bitregister_2 (
    .reset(Reset_out), .Load(control_unit_vhardwired_1_b_wr_en), .CLK(clk_1_o),
    .reg_in(bitregister_1_reg_out), .reg_out_en(control_unit_vhardwired_1_b_rd_en),
    .reg_out(bitregister_1_reg_out), .O5(bitregister_2_o5), .O6(bitregister_2_o6), .O7(bitregister_2_o7),
    .O0(bitregister_2_o0), .O1(bitregister_2_o1), .O2(bitregister_2_o2), .O3(bitregister_2_o3),
    .O4(bitregister_2_o4));
  DotMatrix #(.dotshape("circle"), .inputtype("row"), .matrixcols(1), .matrixrows(8)) dotmatrix_3 (
    .row0(bitregister_3_o0), .row1(bitregister_3_o1), .row2(bitregister_3_o2), .row3(bitregister_3_o3),
    .row4(bitregister_3_o4), .row5(bitregister_3_o5), .row6(bitregister_3_o6), .row7(bitregister_3_o7));
  BitRegister bitregister_3 (
    .reset(Reset_out), .Load(control_unit_vhardwired_1_c_wr_en), .CLK(clk_1_o),
    .reg_in(bitregister_1_reg_out), .reg_out_en(control_unit_vhardwired_1_c_rd_en),
    .reg_out(bitregister_1_reg_out), .O5(bitregister_3_o5), .O6(bitregister_3_o6), .O7(bitregister_3_o7),
    .O0(bitregister_3_o0), .O1(bitregister_3_o1), .O2(bitregister_3_o2), .O3(bitregister_3_o3),
    .O4(bitregister_3_o4));
  DotMatrix #(.dotshape("circle"), .inputtype("row"), .matrixcols(1), .matrixrows(8)) dotmatrix_4 (
    .row0(bitregister_4_o0), .row1(bitregister_4_o1), .row2(bitregister_4_o2), .row3(bitregister_4_o3),
    .row4(bitregister_4_o4), .row5(bitregister_4_o5), .row6(bitregister_4_o6), .row7(bitregister_4_o7));
  BitRegister bitregister_4 (
    .reset(Reset_out), .CLK(clk_1_o), .reg_in(bitregister_1_reg_out), .reg_out_en(1'b1),
    .reg_out(bitregister_4_reg_out), .O5(bitregister_4_o5), .O6(bitregister_4_o6), .O7(bitregister_4_o7),
    .O0(bitregister_4_o0), .O1(bitregister_4_o1), .O2(bitregister_4_o2), .O3(bitregister_4_o3),
    .O4(bitregister_4_o4));  // open: Load
  DotMatrix #(.dotshape("circle"), .inputtype("row"), .matrixcols(1), .matrixrows(8)) dotmatrix_5 (
    .row0(bitregister_5_o0), .row1(bitregister_5_o1), .row2(bitregister_5_o2), .row3(bitregister_5_o3),
    .row4(bitregister_5_o4), .row5(bitregister_5_o5), .row6(bitregister_5_o6), .row7(bitregister_5_o7));
  BitRegister bitregister_5 (
    .reset(Reset_out), .Load(control_unit_vhardwired_1_d_wr_en), .CLK(clk_1_o),
    .reg_in(bitregister_1_reg_out), .reg_out_en(control_unit_vhardwired_1_d_rd_en),
    .reg_out(bitregister_1_reg_out), .O5(bitregister_5_o5), .O6(bitregister_5_o6), .O7(bitregister_5_o7),
    .O0(bitregister_5_o0), .O1(bitregister_5_o1), .O2(bitregister_5_o2), .O3(bitregister_5_o3),
    .O4(bitregister_5_o4));
  DotMatrix #(.dotshape("circle"), .inputtype("row"), .matrixcols(1), .matrixrows(8)) dotmatrix_6 (
    .row0(bitregister_6_o0), .row1(bitregister_6_o1), .row2(bitregister_6_o2), .row3(bitregister_6_o3),
    .row4(bitregister_6_o4), .row5(bitregister_6_o5), .row6(bitregister_6_o6), .row7(bitregister_6_o7));
  BitRegister bitregister_6 (
    .reset(Reset_out), .CLK(clk_1_o), .reg_in(bitregister_1_reg_out), .reg_out_en(1'b1),
    .reg_out(bitregister_6_reg_out), .O5(bitregister_6_o5), .O6(bitregister_6_o6), .O7(bitregister_6_o7),
    .O0(bitregister_6_o0), .O1(bitregister_6_o1), .O2(bitregister_6_o2), .O3(bitregister_6_o3),
    .O4(bitregister_6_o4));  // open: Load
  Hex_Digit_Display hex_digit_display_1 (.value(bitregister_7_reg_out_2));  // open: dp
  Hex_Digit_Display hex_digit_display_2 (.value(bitregister_7_reg_out));  // open: dp
  DotMatrix #(.dotshape("circle"), .matrixcols(8), .matrixrows(1)) dotmatrix_7 (
    .col0(alu_1_s7), .col1(alu_1_s6), .col2(alu_1_s5), .col3(alu_1_s4), .col4(alu_1_s3), .col5(alu_1_s2),
    .col6(alu_1_s1), .col7(alu_1_s0));
  ALU alu_1 (
    .AInput(bitregister_4_reg_out), .BInput(bitregister_6_reg_out), .CF(alu_1_cf), .S7(alu_1_s7),
    .S6(alu_1_s6), .S5(alu_1_s5), .S4(alu_1_s4), .S3(alu_1_s3), .S2(alu_1_s2), .S1(alu_1_s1), .S0(alu_1_s0),
    .ZF(alu_1_zf), .ALU_Out(bitregister_1_reg_out));  // open: out_en, Sub
  DotMatrix #(.dotshape("circle"), .matrixcols(2), .matrixrows(1)) dotmatrix_8 (
    .col0(flagreg_1_zf), .col1(flagreg_1_cf));
  FlagReg flagreg_1 (
    .Clock(clk_1_o), .Carry(alu_1_cf), .Zero(alu_1_zf), .reset(Reset_out), .CF(flagreg_1_cf),
    .ZF(flagreg_1_zf));  // open: Enable, CarryOut, ZeroOut
  ROM rom_1 (.addr(boot_strap_control_unit_1_r_addr), .data(rom_1_data));
  DotMatrix #(.dotshape("circle"), .inputtype("row"), .matrixcols(1), .matrixrows(8)) dotmatrix_9 (
    .row0(bitregister_7_o0), .row1(bitregister_7_o1), .row2(bitregister_7_o2), .row3(bitregister_7_o3),
    .row4(bitregister_7_o4), .row5(bitregister_7_o5), .row6(bitregister_7_o6), .row7(bitregister_7_o7));
  BitRegister bitregister_7 (
    .reset(Reset_out), .CLK(clk_1_o), .reg_in(bitregister_1_reg_out), .reg_out_en(1'b1),
    .reg_out({bitregister_7_reg_out_2, bitregister_7_reg_out}), .O5(bitregister_7_o5), .O6(bitregister_7_o6),
    .O7(bitregister_7_o7), .O0(bitregister_7_o0), .O1(bitregister_7_o1), .O2(bitregister_7_o2),
    .O3(bitregister_7_o3), .O4(bitregister_7_o4));  // open: Load
  DotMatrix #(.dotshape("circle"), .inputtype("row"), .matrixcols(1), .matrixrows(8)) dotmatrix_10 (
    .row0(sram_256_bytes_1_s0), .row1(sram_256_bytes_1_s1), .row2(sram_256_bytes_1_s2),
    .row3(sram_256_bytes_1_s3), .row4(sram_256_bytes_1_s4), .row5(sram_256_bytes_1_s5),
    .row6(sram_256_bytes_1_s6), .row7(sram_256_bytes_1_s7));
  SRAM_256_Bytes sram_256_bytes_1 (
    .A7(bitregister_7_reg_out_2[3]), .A6(bitregister_7_reg_out_2[2]), .A5(bitregister_7_reg_out_2[1]),
    .A4(bitregister_7_reg_out_2[0]), .A3(bitregister_7_reg_out[3]), .A2(bitregister_7_reg_out[2]),
    .A1(bitregister_7_reg_out[1]), .A0(bitregister_7_reg_out[0]), .CLR(Reset_out), .CLK(clk_1_o),
    .I(bitregister_1_reg_out), .S2(sram_256_bytes_1_s2), .S3(sram_256_bytes_1_s3), .S4(sram_256_bytes_1_s4),
    .S5(sram_256_bytes_1_s5), .S6(sram_256_bytes_1_s6), .S7(sram_256_bytes_1_s7), .S0(sram_256_bytes_1_s0),
    .S1(sram_256_bytes_1_s1), .Q(bitregister_1_reg_out));  // open: Write, Read
  Hex_Digit_Display hex_digit_display_3 (.value(bitregister_8_reg_out_2));  // open: dp
  Clk clk_1 (.halt(control_unit_vhardwired_1_halt), .O(clk_1_o));
  Hex_Digit_Display hex_digit_display_4 (.value(bitregister_8_reg_out));  // open: dp
  Multiplexer #(.width(8)) multiplexer_1 (
    .in0(bitregister_1_reg_out), .in1(boot_strap_control_unit_1_o), .out(multiplexer_1_out),
    .sel(boot_strap_control_unit_1_bootstrapmode));
  Counter_8_bts counter_8_bts_1 (
    .PC_OUT(control_unit_vhardwired_1_pc_out), .PC_INC(control_unit_vhardwired_1_pc_inc), .CLK(clk_1_o),
    .PC_RESET(Reset_out), .PC_WRITE(control_unit_vhardwired_1_pc_wr), .I7(bitregister_1_reg_out[7]),
    .I6(bitregister_1_reg_out[6]), .I5(bitregister_1_reg_out[5]), .I4(bitregister_1_reg_out[4]),
    .I3(bitregister_1_reg_out[3]), .I2(bitregister_1_reg_out[2]), .I1(bitregister_1_reg_out[1]),
    .I0(bitregister_1_reg_out[0]), .D7(counter_8_bts_1_d7), .D6(counter_8_bts_1_d6), .D5(counter_8_bts_1_d5),
    .D4(counter_8_bts_1_d4), .D3(counter_8_bts_1_d3), .D2(counter_8_bts_1_d2), .D1(counter_8_bts_1_d1),
    .D0(counter_8_bts_1_d0), .Q(bitregister_1_reg_out));
  Boot_Strap_Control_Unit boot_strap_control_unit_1 (
    .Enable(switch_1_p2), .R_DATA(rom_1_data), .CLK(clk_1_o),
    .BootStrapMode(boot_strap_control_unit_1_bootstrapmode), .RAM_WR(boot_strap_control_unit_1_ram_wr),
    .REG_RD(boot_strap_control_unit_1_reg_rd), .R_ADDR(boot_strap_control_unit_1_r_addr),
    .O(boot_strap_control_unit_1_o));
  DotMatrix #(.dotshape("circle"), .inputtype("row"), .matrixcols(1), .matrixrows(8)) dotmatrix_11 (
    .row0(bitregister_8_o0), .row1(bitregister_8_o1), .row2(bitregister_8_o2), .row3(bitregister_8_o3),
    .row4(bitregister_8_o4), .row5(bitregister_8_o5), .row6(bitregister_8_o6), .row7(bitregister_8_o7));
  BitRegister bitregister_8 (
    .reset(Reset_out), .Load(or_1_out), .CLK(clk_1_o), .reg_in(multiplexer_1_out), .reg_out_en(1'b1),
    .reg_out({bitregister_8_reg_out_2, bitregister_8_reg_out}), .O5(bitregister_8_o5), .O6(bitregister_8_o6),
    .O7(bitregister_8_o7), .O0(bitregister_8_o0), .O1(bitregister_8_o1), .O2(bitregister_8_o2),
    .O3(bitregister_8_o3), .O4(bitregister_8_o4));
  or or_1 (or_1_out, boot_strap_control_unit_1_reg_rd, and_1_out);
  DotMatrix #(.dotshape("circle"), .inputtype("row"), .matrixcols(1), .matrixrows(8)) dotmatrix_12 (
    .row0(counter_8_bts_1_d0), .row1(counter_8_bts_1_d1), .row2(counter_8_bts_1_d2),
    .row3(counter_8_bts_1_d3), .row4(counter_8_bts_1_d4), .row5(counter_8_bts_1_d5),
    .row6(counter_8_bts_1_d6), .row7(counter_8_bts_1_d7));
  and and_1 (and_1_out, ~boot_strap_control_unit_1_bootstrapmode, control_unit_vhardwired_1_mar_in);  // AND_Gate
  _7_Segment_Display u_7_segment_display_1 (
    .g(bit_to_7segment_1_g3), .f(bit_to_7segment_1_f3), .a(bit_to_7segment_1_a3), .b(bit_to_7segment_1_b3),
    .e(bit_to_7segment_1_e3), .d(bit_to_7segment_1_d3), .c(bit_to_7segment_1_c3));  // open: dp
  _7_Segment_Display u_7_segment_display_2 (
    .g(bit_to_7segment_1_g2), .f(bit_to_7segment_1_f2), .a(bit_to_7segment_1_a2), .b(bit_to_7segment_1_b2),
    .e(bit_to_7segment_1_e2), .d(bit_to_7segment_1_d2), .c(bit_to_7segment_1_c2));  // open: dp
  Button Reset (.out(Reset_out));
  DotMatrix #(.dotshape("circle"), .inputtype("row"), .matrixcols(1), .matrixrows(8)) dotmatrix_13 (
    .row0(sram_256_bytes_2_s0), .row1(sram_256_bytes_2_s1), .row2(sram_256_bytes_2_s2),
    .row3(sram_256_bytes_2_s3), .row4(sram_256_bytes_2_s4), .row5(sram_256_bytes_2_s5),
    .row6(sram_256_bytes_2_s6), .row7(sram_256_bytes_2_s7));
  SRAM_256_Bytes sram_256_bytes_2 (
    .A7(bitregister_8_reg_out_2[3]), .A6(bitregister_8_reg_out_2[2]), .A5(bitregister_8_reg_out_2[1]),
    .A4(bitregister_8_reg_out_2[0]), .A3(bitregister_8_reg_out[3]), .A2(bitregister_8_reg_out[2]),
    .A1(bitregister_8_reg_out[1]), .A0(bitregister_8_reg_out[0]), .CLR(switch_1_p2),
    .Write(boot_strap_control_unit_1_ram_wr), .CLK(clk_1_o), .I(boot_strap_control_unit_1_o),
    .Read(control_unit_vhardwired_1_ir), .S2(sram_256_bytes_2_s2), .S3(sram_256_bytes_2_s3),
    .S4(sram_256_bytes_2_s4), .S5(sram_256_bytes_2_s5), .S6(sram_256_bytes_2_s6), .S7(sram_256_bytes_2_s7),
    .S0(sram_256_bytes_2_s0), .S1(sram_256_bytes_2_s1), .Q(bitregister_1_reg_out));
  _7_Segment_Display #(.decimalPoint("false")) u_7_segment_display_3 (
    .g(bit_to_7segment_1_g1), .f(bit_to_7segment_1_f1), .a(bit_to_7segment_1_a1), .b(bit_to_7segment_1_b1),
    .e(bit_to_7segment_1_e1), .d(bit_to_7segment_1_d1), .c(bit_to_7segment_1_c1));
  Bit_to_7Segment bit_to_7segment_1 (
    .I(bitregister_9_reg_out), .a1(bit_to_7segment_1_a1), .b1(bit_to_7segment_1_b1),
    .c1(bit_to_7segment_1_c1), .d1(bit_to_7segment_1_d1), .e1(bit_to_7segment_1_e1),
    .f1(bit_to_7segment_1_f1), .g1(bit_to_7segment_1_g1), .a2(bit_to_7segment_1_a2),
    .b2(bit_to_7segment_1_b2), .c2(bit_to_7segment_1_c2), .d2(bit_to_7segment_1_d2),
    .e2(bit_to_7segment_1_e2), .f2(bit_to_7segment_1_f2), .g2(bit_to_7segment_1_g2),
    .a3(bit_to_7segment_1_a3), .b3(bit_to_7segment_1_b3), .c3(bit_to_7segment_1_c3),
    .d3(bit_to_7segment_1_d3), .e3(bit_to_7segment_1_e3), .f3(bit_to_7segment_1_f3), .g3(bit_to_7segment_1_g3));
  BitRegister bitregister_9 (
    .reset(Reset_out), .CLK(clk_1_o), .reg_in(bitregister_1_reg_out), .reg_out_en(1'b1),
    .reg_out(bitregister_9_reg_out), .O5(bitregister_9_o5), .O6(bitregister_9_o6), .O7(bitregister_9_o7),
    .O0(bitregister_9_o0), .O1(bitregister_9_o1), .O2(bitregister_9_o2), .O3(bitregister_9_o3),
    .O4(bitregister_9_o4));  // open: Load
  // Switch switch_1: pin names not known; wires that end beside it: Reset_out, switch_1_p2
  DotMatrix #(.dotshape("circle"), .inputtype("row"), .matrixcols(1), .matrixrows(8)) dotmatrix_14 (
    .row0(bitregister_9_o0), .row1(bitregister_9_o1), .row2(bitregister_9_o2), .row3(bitregister_9_o3),
    .row4(bitregister_9_o4), .row5(bitregister_9_o5), .row6(bitregister_9_o6), .row7(bitregister_9_o7));

  // Notes on the sheet:
  //   RegisterA
  //   Register B
  //   Register C
  //   Accumulator A
  //   Register D
  //   Accumulator B
  //   DMAR
  //   contents of rom_1 (hex, n*v repeats v):
  //   5c cc 43 dc 12*0 ec 10 ff
  //   IMAR
  //   PC
  //   Output Register
endmodule

module ALU (
  input  out_en,
  input  Sub,
  input  [7:0] AInput,
  input  [7:0] BInput,
  output ZF,
  output CF,
  output [7:0] ALU_Out,
  output S7,
  output S6,
  output S5,
  output S4,
  output S3,
  output S2,
  output S1,
  output S0
);

  wire and_1_out, and_2_out, and_3_out, and_4_out, and_5_out, and_6_out, and_7_out, and_8_out, and_9_out,
       and_10_out, and_11_out, and_12_out, and_13_out, and_14_out, and_15_out, and_16_out, nor_1_out,
       nor_2_out, nor_3_out, nor_4_out, nor_5_out, nor_6_out, nor_7_out, nor_8_out, nor_9_out, nor_10_out,
       nor_11_out, nor_12_out, or_1_out, or_2_out, or_3_out, or_4_out, or_5_out, or_6_out, or_7_out,
       xor_1_out, xor_2_out, xor_3_out, xor_4_out, xor_5_out, xor_6_out, xor_7_out, xor_8_out, xor_9_out,
       xor_10_out, xor_11_out, xor_12_out, xor_13_out, xor_14_out, xor_15_out, xor_16_out;

  xor xor_1 (xor_1_out, Sub, BInput[1]);
  xor xor_2 (xor_2_out, Sub, BInput[5]);
  xor xor_3 (xor_3_out, Sub, BInput[0]);
  xor xor_4 (xor_4_out, Sub, BInput[2]);
  xor xor_5 (xor_5_out, Sub, BInput[3]);
  xor xor_6 (xor_6_out, Sub, BInput[4]);
  xor xor_7 (xor_7_out, Sub, BInput[6]);
  xor xor_8 (xor_8_out, Sub, BInput[7]);
  xor xor_9 (xor_9_out, AInput[0], xor_3_out);
  and and_1 (and_1_out, AInput[0], xor_3_out);
  xor xor_10 (xor_10_out, AInput[1], xor_1_out);
  and and_2 (and_2_out, AInput[1], xor_1_out);
  xor xor_11 (xor_11_out, AInput[2], xor_4_out);
  and and_3 (and_3_out, AInput[2], xor_4_out);
  xor xor_12 (xor_12_out, AInput[3], xor_5_out);
  and and_4 (and_4_out, AInput[3], xor_5_out);
  xor xor_13 (xor_13_out, AInput[4], xor_6_out);
  and and_5 (and_5_out, AInput[4], xor_6_out);
  xor xor_14 (xor_14_out, AInput[5], xor_2_out);
  and and_6 (and_6_out, AInput[5], xor_2_out);
  xor xor_15 (xor_15_out, AInput[6], xor_7_out);
  and and_7 (and_7_out, AInput[6], xor_7_out);
  xor xor_16 (xor_16_out, AInput[7], xor_8_out);
  and and_8 (and_8_out, AInput[7], xor_8_out);
  xor xor_17 (S0, xor_9_out, Sub);
  and and_9 (and_9_out, xor_9_out, Sub);
  xor xor_18 (S1, xor_10_out, or_1_out);
  and and_10 (and_10_out, xor_10_out, or_1_out);
  xor xor_19 (S4, xor_13_out, or_6_out);
  and and_11 (and_11_out, xor_13_out, or_6_out);
  xor xor_20 (S5, xor_14_out, or_3_out);
  and and_12 (and_12_out, xor_14_out, or_3_out);
  or or_1 (or_1_out, and_9_out, and_1_out);
  or or_2 (or_2_out, and_10_out, and_2_out);
  xor xor_21 (S2, xor_11_out, or_2_out);
  and and_13 (and_13_out, xor_11_out, or_2_out);
  xor xor_22 (S3, xor_12_out, or_5_out);
  and and_14 (and_14_out, xor_12_out, or_5_out);
  or or_3 (or_3_out, and_11_out, and_5_out);
  or or_4 (or_4_out, and_12_out, and_6_out);
  xor xor_23 (S6, xor_15_out, or_4_out);
  and and_15 (and_15_out, xor_15_out, or_4_out);
  xor xor_24 (S7, xor_16_out, or_7_out);
  and and_16 (and_16_out, xor_16_out, or_7_out);
  or or_5 (or_5_out, and_13_out, and_3_out);
  or or_6 (or_6_out, and_14_out, and_4_out);
  or or_7 (or_7_out, and_15_out, and_7_out);
  or or_8 (CF, and_16_out, and_8_out);
  nor nor_1 (nor_1_out, S0, S1);
  nor nor_2 (nor_2_out, S2, S3);
  nor nor_3 (nor_3_out, S4, S5);
  nor nor_4 (nor_4_out, S6, S7);
  nor nor_5 (nor_5_out, nor_1_out, nor_1_out);
  nor nor_6 (nor_6_out, nor_2_out, nor_2_out);
  nor nor_7 (nor_7_out, nor_3_out, nor_3_out);
  nor nor_8 (nor_8_out, nor_4_out, nor_4_out);
  TriStateBuffer tristatebuffer_1 (
    .Enable(out_en), .I0(S0), .I1(S1), .I2(S2), .I3(S3), .I4(S4), .I5(S5), .I6(S6), .I7(S7), .O0(ALU_Out[0]),
    .O1(ALU_Out[1]), .O2(ALU_Out[2]), .O3(ALU_Out[3]), .O4(ALU_Out[4]), .O5(ALU_Out[5]), .O6(ALU_Out[6]),
    .O7(ALU_Out[7]));
  nor nor_9 (nor_9_out, nor_5_out, nor_6_out);
  nor nor_10 (nor_10_out, nor_7_out, nor_8_out);
  nor nor_11 (nor_11_out, nor_9_out, nor_9_out);
  nor nor_12 (nor_12_out, nor_10_out, nor_10_out);
  nor nor_13 (ZF, nor_11_out, nor_12_out);
endmodule

module Clk (
  input  halt,
  output O
);

  wire clock_1_out, not_1_out;

  Clock clock_1 (.out(clock_1_out));
  not not_1 (not_1_out, halt);
  and and_1 (O, clock_1_out, not_1_out);
endmodule

module SR_Latch (
  input  R,
  input  S,
  output Q,
  output Qi
);

  nor nor_1 (Q, R, Qi);
  nor nor_2 (Qi, Q, S);
endmodule

module D_Latch (
  input  reset,
  input  en,
  input  input_bit,
  output Q,
  output Qi
);

  wire and_1_out, and_2_out, not_1_out, or_1_out;

  not not_1 (not_1_out, input_bit);
  and and_1 (and_1_out, not_1_out, en);
  and and_2 (and_2_out, en, input_bit);
  or or_1 (or_1_out, reset, and_1_out);
  SR_Latch sr_latch_1 (.R(or_1_out), .S(and_2_out), .Q(Q), .Qi(Qi));
endmodule

module D_FF (
  input  reset,
  input  CLK,
  input  D,
  output Q,
  output Qi
);

  wire and_1_out, not_1_out, not_2_out, not_3_out;

  not not_1 (not_1_out, CLK);
  not not_2 (not_2_out, not_1_out);
  not not_3 (not_3_out, not_2_out);
  and and_1 (and_1_out, CLK, not_3_out);
  D_Latch d_latch_1 (.reset(reset), .en(and_1_out), .input_bit(D), .Q(Q), .Qi(Qi));
endmodule

module BitRegister (
  input  reset,
  input  Load,
  input  CLK,
  input  reg_out_en,
  input  [7:0] reg_in,
  output O0,
  output O1,
  output O2,
  output O3,
  output O4,
  output O5,
  output O6,
  output O7,
  output [7:0] reg_out
);

  wire and_1_out, and_2_out, and_3_out, and_4_out, and_5_out, and_6_out, and_7_out, and_8_out, and_9_out,
       and_10_out, and_11_out, and_12_out, and_13_out, and_14_out, and_15_out, and_16_out, buffer_1_out,
       d_ff_1_q, d_ff_2_q, d_ff_3_q, d_ff_4_q, d_ff_5_q, d_ff_6_q, d_ff_7_q, d_ff_8_q, not_1_out, or_1_out,
       or_2_out, or_3_out, or_4_out, or_5_out, or_6_out, or_7_out, or_8_out;

  buf buffer_1 (buffer_1_out, Load);
  not not_1 (not_1_out, Load);
  and and_1 (and_1_out, d_ff_1_q, not_1_out);
  and and_2 (and_2_out, buffer_1_out, reg_in[0]);
  and and_3 (and_3_out, d_ff_2_q, not_1_out);
  and and_4 (and_4_out, buffer_1_out, reg_in[1]);
  and and_5 (and_5_out, d_ff_3_q, not_1_out);
  and and_6 (and_6_out, buffer_1_out, reg_in[2]);
  and and_7 (and_7_out, d_ff_4_q, not_1_out);
  and and_8 (and_8_out, buffer_1_out, reg_in[3]);
  and and_9 (and_9_out, d_ff_5_q, not_1_out);
  and and_10 (and_10_out, buffer_1_out, reg_in[4]);
  and and_11 (and_11_out, d_ff_6_q, not_1_out);
  and and_12 (and_12_out, buffer_1_out, reg_in[5]);
  and and_13 (and_13_out, d_ff_7_q, not_1_out);
  and and_14 (and_14_out, buffer_1_out, reg_in[6]);
  and and_15 (and_15_out, d_ff_8_q, not_1_out);
  and and_16 (and_16_out, buffer_1_out, reg_in[7]);
  or or_1 (or_1_out, and_1_out, and_2_out);
  or or_2 (or_2_out, and_3_out, and_4_out);
  or or_3 (or_3_out, and_5_out, and_6_out);
  or or_4 (or_4_out, and_7_out, and_8_out);
  or or_5 (or_5_out, and_9_out, and_10_out);
  or or_6 (or_6_out, and_11_out, and_12_out);
  or or_7 (or_7_out, and_13_out, and_14_out);
  or or_8 (or_8_out, and_15_out, and_16_out);
  D_Flip_Flop d_ff_1 (.D(or_1_out), .clk(CLK), .Q(d_ff_1_q), .reset(reset));  // open: Qn, preset
  D_Flip_Flop d_ff_2 (.D(or_2_out), .clk(CLK), .Q(d_ff_2_q), .reset(reset));  // open: Qn, preset
  D_Flip_Flop d_ff_3 (.D(or_3_out), .clk(CLK), .Q(d_ff_3_q), .reset(reset));  // open: Qn, preset
  D_Flip_Flop d_ff_4 (.D(or_4_out), .clk(CLK), .Q(d_ff_4_q), .reset(reset));  // open: Qn, preset
  D_Flip_Flop d_ff_5 (.D(or_5_out), .clk(CLK), .Q(d_ff_5_q), .reset(reset));  // open: Qn, preset
  D_Flip_Flop d_ff_6 (.D(or_6_out), .clk(CLK), .Q(d_ff_6_q), .reset(reset));  // open: Qn, preset
  D_Flip_Flop d_ff_7 (.D(or_7_out), .clk(CLK), .Q(d_ff_7_q), .reset(reset));  // open: Qn, preset
  D_Flip_Flop d_ff_8 (.D(or_8_out), .clk(CLK), .Q(d_ff_8_q), .reset(reset));  // open: Qn, preset
  buf buffer_2 (O0, d_ff_1_q);
  buf buffer_3 (O1, d_ff_2_q);
  buf buffer_4 (O2, d_ff_3_q);
  buf buffer_5 (O3, d_ff_4_q);
  buf buffer_6 (O4, d_ff_5_q);
  buf buffer_7 (O5, d_ff_6_q);
  buf buffer_8 (O6, d_ff_7_q);
  buf buffer_9 (O7, d_ff_8_q);
  TriStateBuffer tristatebuffer_1 (
    .Enable(reg_out_en), .I0(d_ff_1_q), .I1(d_ff_2_q), .I2(d_ff_3_q), .I3(d_ff_4_q), .I4(d_ff_5_q),
    .I5(d_ff_6_q), .I6(d_ff_7_q), .I7(d_ff_8_q), .O0(reg_out[0]), .O1(reg_out[1]), .O2(reg_out[2]),
    .O3(reg_out[3]), .O4(reg_out[4]), .O5(reg_out[5]), .O6(reg_out[6]), .O7(reg_out[7]));
endmodule

module FlagReg (
  input  reset,
  input  Enable,
  input  Clock,
  input  Carry,
  input  Zero,
  output CF,
  output CarryOut,
  output ZF,
  output ZeroOut
);

  wire and_1_out, and_2_out, and_3_out, and_4_out, buffer_1_out, not_1_out, or_1_out, or_2_out;

  buf buffer_1 (buffer_1_out, Enable);
  not not_1 (not_1_out, Enable);
  and and_1 (and_1_out, CarryOut, not_1_out);
  and and_2 (and_2_out, Carry, buffer_1_out);
  and and_3 (and_3_out, ZeroOut, not_1_out);
  and and_4 (and_4_out, Zero, buffer_1_out);
  or or_1 (or_1_out, and_1_out, and_2_out);
  or or_2 (or_2_out, and_3_out, and_4_out);
  D_Flip_Flop d_ff_1 (.D(or_1_out), .clk(Clock), .Q(CarryOut), .reset(reset));  // open: Qn, preset
  D_Flip_Flop d_ff_2 (.D(or_2_out), .clk(Clock), .Q(ZeroOut), .reset(reset));  // open: Qn, preset

  assign CF = CarryOut;
  assign ZF = ZeroOut;
endmodule

module TriStateBuffer (
  input  Enable,
  input  I0,
  input  I1,
  input  I2,
  input  I3,
  input  I4,
  input  I5,
  input  I6,
  input  I7,
  output O0,
  output O1,
  output O2,
  output O3,
  output O4,
  output O5,
  output O6,
  output O7
);

  assign O0 = Enable ? I0 : 1'bz;  // Controlled_Buffer controlled_buffer_1
  assign O1 = Enable ? I1 : 1'bz;  // Controlled_Buffer controlled_buffer_2
  assign O2 = Enable ? I2 : 1'bz;  // Controlled_Buffer controlled_buffer_3
  assign O3 = Enable ? I3 : 1'bz;  // Controlled_Buffer controlled_buffer_4
  assign O4 = Enable ? I4 : 1'bz;  // Controlled_Buffer controlled_buffer_5
  assign O5 = Enable ? I5 : 1'bz;  // Controlled_Buffer controlled_buffer_6
  assign O6 = Enable ? I6 : 1'bz;  // Controlled_Buffer controlled_buffer_7
  assign O7 = Enable ? I7 : 1'bz;  // Controlled_Buffer controlled_buffer_8
endmodule

module Reverser (
  input  I7,
  input  I6,
  input  I5,
  input  I4,
  input  I3,
  input  I2,
  input  I1,
  input  I0,
  output O0,
  output O1,
  output O2,
  output O3,
  output O4,
  output O5,
  output O6,
  output O7
);


  assign O0 = I0;
  assign O1 = I1;
  assign O2 = I2;
  assign O3 = I3;
  assign O4 = I4;
  assign O5 = I5;
  assign O6 = I6;
  assign O7 = I7;
endmodule

module JK_flipflop (
  input  R,
  input  K,
  input  CLK,
  input  J,
  input  S,
  output Q,
  output Qi
);

  wire and_1_out, and_2_out, and_3_out, and_4_out, and_5_out, not_1_out, not_2_out, not_3_out, or_1_out,
       or_2_out;

  not not_1 (not_1_out, CLK);
  not not_2 (not_2_out, not_1_out);
  not not_3 (not_3_out, not_2_out);
  and and_1 (and_1_out, CLK, not_3_out);
  and and_2 (and_2_out, Q, K);
  and and_3 (and_3_out, and_1_out, J);
  and and_4 (and_4_out, and_2_out, and_1_out);
  and and_5 (and_5_out, and_3_out, Qi);
  or or_1 (or_1_out, R, and_4_out);
  or or_2 (or_2_out, and_5_out, S);
  nor nor_1 (Q, or_1_out, Qi);
  nor nor_2 (Qi, Q, or_2_out);
endmodule

module Counter_8_bts (
  input  PC_OUT,
  input  PC_INC,
  input  CLK,
  input  PC_RESET,
  input  PC_WRITE,
  input  I7,
  input  I6,
  input  I5,
  input  I4,
  input  I3,
  input  I2,
  input  I1,
  input  I0,
  output [7:0] Q,
  output D7,
  output D6,
  output D5,
  output D4,
  output D3,
  output D2,
  output D1,
  output D0
);

  wire and_1_out, and_2_out, and_3_out, and_4_out, and_5_out, and_6_out, and_7_out, and_8_out, and_9_out,
       and_10_out, and_11_out, and_12_out, and_13_out, and_14_out, and_15_out, and_16_out, and_17_out,
       and_18_out, and_19_out, and_20_out, and_21_out, and_22_out, and_23_out, and_24_out, and_25_out,
       and_26_out, and_27_out, and_28_out, and_29_out, and_30_out, and_31_out, and_32_out, j_k_ff_2_qn,
       j_k_ff_3_qn, j_k_ff_4_qn, j_k_ff_5_qn, j_k_ff_6_qn, j_k_ff_7_qn, j_k_ff_8_qn, or_1_out, or_2_out,
       or_3_out, or_4_out, or_5_out, or_6_out, or_7_out, or_8_out;

  and and_1 (and_1_out, PC_WRITE, I7);
  J_K_Flip_Flop j_k_ff_1 (
    .J(PC_INC), .K(PC_INC), .clk(j_k_ff_2_qn), .Q(D7), .preset(and_2_out), .reset(or_1_out));  // open: Qn
  or or_1 (or_1_out, PC_RESET, and_3_out);
  and and_2 (and_2_out, and_1_out, CLK);
  and and_3 (and_3_out, and_4_out, CLK);
  and and_4 (and_4_out, PC_WRITE, ~I7);  // AND_Gate
  and and_5 (and_5_out, PC_WRITE, I6);
  J_K_Flip_Flop j_k_ff_2 (
    .J(PC_INC), .K(PC_INC), .clk(j_k_ff_3_qn), .Q(D6), .Qn(j_k_ff_2_qn), .preset(and_6_out), .reset(or_2_out));
  or or_2 (or_2_out, PC_RESET, and_7_out);
  and and_6 (and_6_out, and_5_out, CLK);
  and and_7 (and_7_out, and_8_out, CLK);
  and and_8 (and_8_out, PC_WRITE, ~I6);  // AND_Gate
  J_K_Flip_Flop j_k_ff_3 (
    .J(PC_INC), .K(PC_INC), .clk(j_k_ff_4_qn), .Q(D5), .Qn(j_k_ff_3_qn), .preset(and_9_out), .reset(or_3_out));
  or or_3 (or_3_out, PC_RESET, and_10_out);
  and and_9 (and_9_out, and_11_out, CLK);
  and and_10 (and_10_out, and_12_out, CLK);
  and and_11 (and_11_out, PC_WRITE, I5);
  and and_12 (and_12_out, PC_WRITE, ~I5);  // AND_Gate
  J_K_Flip_Flop j_k_ff_4 (
    .J(PC_INC), .K(PC_INC), .clk(j_k_ff_5_qn), .Q(D4), .Qn(j_k_ff_4_qn), .preset(and_13_out), .reset(or_4_out));
  or or_4 (or_4_out, PC_RESET, and_14_out);
  and and_13 (and_13_out, and_15_out, CLK);
  and and_14 (and_14_out, and_16_out, CLK);
  and and_15 (and_15_out, PC_WRITE, I4);
  and and_16 (and_16_out, PC_WRITE, ~I4);  // AND_Gate
  J_K_Flip_Flop j_k_ff_5 (
    .J(PC_INC), .K(PC_INC), .clk(j_k_ff_6_qn), .Q(D3), .Qn(j_k_ff_5_qn), .preset(and_17_out), .reset(or_5_out));
  or or_5 (or_5_out, PC_RESET, and_20_out);
  and and_17 (and_17_out, and_18_out, CLK);
  and and_18 (and_18_out, PC_WRITE, I3);
  and and_19 (and_19_out, PC_WRITE, ~I3);  // AND_Gate
  J_K_Flip_Flop j_k_ff_6 (
    .J(PC_INC), .K(PC_INC), .clk(j_k_ff_7_qn), .Q(D2), .Qn(j_k_ff_6_qn), .preset(and_21_out), .reset(or_6_out));
  and and_20 (and_20_out, and_19_out, CLK);
  and and_21 (and_21_out, and_22_out, CLK);
  and and_22 (and_22_out, PC_WRITE, I2);
  J_K_Flip_Flop j_k_ff_7 (
    .J(PC_INC), .K(PC_INC), .clk(j_k_ff_8_qn), .Q(D1), .Qn(j_k_ff_7_qn), .preset(and_24_out), .reset(or_7_out));
  or or_6 (or_6_out, PC_RESET, and_23_out);
  and and_23 (and_23_out, and_25_out, CLK);
  and and_24 (and_24_out, and_26_out, CLK);
  and and_25 (and_25_out, PC_WRITE, ~I2);  // AND_Gate
  and and_26 (and_26_out, PC_WRITE, I1);
  or or_7 (or_7_out, PC_RESET, and_27_out);
  and and_27 (and_27_out, and_29_out, CLK);
  and and_28 (and_28_out, and_30_out, CLK);
  and and_29 (and_29_out, PC_WRITE, ~I1);  // AND_Gate
  and and_30 (and_30_out, PC_WRITE, I0);
  J_K_Flip_Flop j_k_ff_8 (
    .J(PC_INC), .K(PC_INC), .clk(CLK), .Q(D0), .Qn(j_k_ff_8_qn), .preset(and_28_out), .reset(or_8_out));
  or or_8 (or_8_out, PC_RESET, and_31_out);
  and and_31 (and_31_out, and_32_out, CLK);
  and and_32 (and_32_out, PC_WRITE, ~I0);  // AND_Gate
  TriStateBuffer tristatebuffer_1 (
    .Enable(PC_OUT), .I0(D0), .I1(D1), .I2(D2), .I3(D3), .I4(D4), .I5(D5), .I6(D6), .I7(D7), .O0(Q[0]),
    .O1(Q[1]), .O2(Q[2]), .O3(Q[3]), .O4(Q[4]), .O5(Q[5]), .O6(Q[6]), .O7(Q[7]));
endmodule

module Adress_decoder_4bts (
  input  A4,
  input  A3,
  input  A2,
  input  A1,
  input  en,
  output DF,
  output DE,
  output DD,
  output DC,
  output DB,
  output DA,
  output D9,
  output D8,
  output D7,
  output D6,
  output D5,
  output D4,
  output D3,
  output D2,
  output D1,
  output D0
);

  wire and_1_out, and_2_out, and_3_out, and_4_out, and_5_out, and_6_out, and_7_out, and_8_out, and_9_out,
       and_10_out, and_11_out, and_12_out, and_13_out, and_14_out, and_15_out, and_16_out, and_17_out,
       and_18_out, and_19_out, and_20_out, and_21_out, and_22_out, and_23_out, and_24_out, and_25_out,
       and_26_out, and_27_out, and_28_out, and_29_out, and_30_out, and_31_out, and_32_out, and_33_out,
       and_34_out, and_35_out, and_36_out, and_37_out, and_38_out, and_39_out, and_40_out, and_41_out,
       and_42_out, and_43_out, and_44_out, and_45_out, and_46_out, and_47_out, and_48_out, not_1_out,
       not_2_out, not_3_out, not_4_out;

  not not_1 (not_1_out, A4);
  not not_2 (not_2_out, A3);
  not not_3 (not_3_out, A2);
  not not_4 (not_4_out, A1);
  and and_1 (and_1_out, not_1_out, not_2_out);
  and and_2 (and_2_out, not_3_out, not_4_out);
  and and_3 (and_3_out, not_1_out, not_2_out);
  and and_4 (and_4_out, not_3_out, A1);
  and and_5 (and_5_out, not_1_out, not_2_out);
  and and_6 (and_6_out, A2, not_4_out);
  and and_7 (and_7_out, not_1_out, not_2_out);
  and and_8 (and_8_out, A2, A1);
  and and_9 (and_9_out, not_1_out, A3);
  and and_10 (and_10_out, not_3_out, not_4_out);
  and and_11 (and_11_out, not_1_out, A3);
  and and_12 (and_12_out, not_3_out, A1);
  and and_13 (and_13_out, not_1_out, A3);
  and and_14 (and_14_out, A2, not_4_out);
  and and_15 (and_15_out, not_1_out, A3);
  and and_16 (and_16_out, A2, A1);
  and and_17 (and_17_out, and_1_out, and_2_out);
  and and_18 (and_18_out, and_3_out, and_4_out);
  and and_19 (and_19_out, and_5_out, and_6_out);
  and and_20 (and_20_out, and_7_out, and_8_out);
  and and_21 (and_21_out, and_9_out, and_10_out);
  and and_22 (and_22_out, and_11_out, and_12_out);
  and and_23 (and_23_out, and_13_out, and_14_out);
  and and_24 (and_24_out, and_15_out, and_16_out);
  assign DF = en ? and_48_out : 1'bz;  // Controlled_Buffer controlled_buffer_1
  assign DE = en ? and_47_out : 1'bz;  // Controlled_Buffer controlled_buffer_2
  assign DD = en ? and_46_out : 1'bz;  // Controlled_Buffer controlled_buffer_3
  assign DC = en ? and_45_out : 1'bz;  // Controlled_Buffer controlled_buffer_4
  assign DB = en ? and_44_out : 1'bz;  // Controlled_Buffer controlled_buffer_5
  assign DA = en ? and_43_out : 1'bz;  // Controlled_Buffer controlled_buffer_6
  assign D9 = en ? and_42_out : 1'bz;  // Controlled_Buffer controlled_buffer_7
  assign D8 = en ? and_41_out : 1'bz;  // Controlled_Buffer controlled_buffer_8
  assign D7 = en ? and_24_out : 1'bz;  // Controlled_Buffer controlled_buffer_9
  assign D6 = en ? and_23_out : 1'bz;  // Controlled_Buffer controlled_buffer_10
  assign D5 = en ? and_22_out : 1'bz;  // Controlled_Buffer controlled_buffer_11
  assign D4 = en ? and_21_out : 1'bz;  // Controlled_Buffer controlled_buffer_12
  assign D3 = en ? and_20_out : 1'bz;  // Controlled_Buffer controlled_buffer_13
  assign D2 = en ? and_19_out : 1'bz;  // Controlled_Buffer controlled_buffer_14
  assign D1 = en ? and_18_out : 1'bz;  // Controlled_Buffer controlled_buffer_15
  assign D0 = en ? and_17_out : 1'bz;  // Controlled_Buffer controlled_buffer_16
  and and_25 (and_25_out, A4, not_2_out);
  and and_26 (and_26_out, not_3_out, not_4_out);
  and and_27 (and_27_out, A4, not_2_out);
  and and_28 (and_28_out, not_3_out, A1);
  and and_29 (and_29_out, A4, not_2_out);
  and and_30 (and_30_out, A2, not_4_out);
  and and_31 (and_31_out, A4, not_2_out);
  and and_32 (and_32_out, A2, A1);
  and and_33 (and_33_out, A4, A3);
  and and_34 (and_34_out, not_3_out, not_4_out);
  and and_35 (and_35_out, A4, A3);
  and and_36 (and_36_out, not_3_out, A1);
  and and_37 (and_37_out, A4, A3);
  and and_38 (and_38_out, A2, not_4_out);
  and and_39 (and_39_out, A4, A3);
  and and_40 (and_40_out, A2, A1);
  and and_41 (and_41_out, and_25_out, and_26_out);
  and and_42 (and_42_out, and_27_out, and_28_out);
  and and_43 (and_43_out, and_29_out, and_30_out);
  and and_44 (and_44_out, and_31_out, and_32_out);
  and and_45 (and_45_out, and_33_out, and_34_out);
  and and_46 (and_46_out, and_35_out, and_36_out);
  and and_47 (and_47_out, and_37_out, and_38_out);
  and and_48 (and_48_out, and_39_out, and_40_out);

  // Notes on the sheet:
  //   easter egg!
endmodule

module SRAM_16_Bytes (
  input  [7:0] D,
  input  Read,
  input  A4,
  input  A3,
  input  A2,
  input  A1,
  input  Enable,
  input  Write,
  input  clear,
  input  CLK,
  output [7:0] Q,
  output S7,
  output S6,
  output S5,
  output S4,
  output S3,
  output S2,
  output S1,
  output S0
);

  wire adress_decoder_4bts_1_d0, adress_decoder_4bts_1_d1, adress_decoder_4bts_1_d2,
       adress_decoder_4bts_1_d3, adress_decoder_4bts_1_d4, adress_decoder_4bts_1_d5,
       adress_decoder_4bts_1_d6, adress_decoder_4bts_1_d7, adress_decoder_4bts_1_d8,
       adress_decoder_4bts_1_d9, adress_decoder_4bts_1_da, adress_decoder_4bts_1_db,
       adress_decoder_4bts_1_dc, adress_decoder_4bts_1_dd, adress_decoder_4bts_1_de,
       adress_decoder_4bts_1_df, and_1_out, and_2_out, and_3_out, and_4_out, and_5_out, and_6_out, and_7_out,
       and_8_out, and_9_out, and_10_out, and_11_out, and_12_out, and_13_out, and_14_out, and_15_out,
       and_16_out, bitregister_1_o0, bitregister_1_o1, bitregister_1_o2, bitregister_1_o3, bitregister_1_o4,
       bitregister_1_o5, bitregister_1_o6, bitregister_1_o7, bitregister_2_o0, bitregister_2_o1,
       bitregister_2_o2, bitregister_2_o3, bitregister_2_o4, bitregister_2_o5, bitregister_2_o6,
       bitregister_2_o7, bitregister_3_o0, bitregister_3_o1, bitregister_3_o2, bitregister_3_o3,
       bitregister_3_o4, bitregister_3_o5, bitregister_3_o6, bitregister_3_o7, bitregister_4_o0,
       bitregister_4_o1, bitregister_4_o2, bitregister_4_o3, bitregister_4_o4, bitregister_4_o5,
       bitregister_4_o6, bitregister_4_o7, bitregister_5_o0, bitregister_5_o1, bitregister_5_o2,
       bitregister_5_o3, bitregister_5_o4, bitregister_5_o5, bitregister_5_o6, bitregister_5_o7,
       bitregister_6_o0, bitregister_6_o1, bitregister_6_o2, bitregister_6_o3, bitregister_6_o4,
       bitregister_6_o5, bitregister_6_o6, bitregister_6_o7, bitregister_7_o0, bitregister_7_o1,
       bitregister_7_o2, bitregister_7_o3, bitregister_7_o4, bitregister_7_o5, bitregister_7_o6,
       bitregister_7_o7, bitregister_8_o0, bitregister_8_o1, bitregister_8_o2, bitregister_8_o3,
       bitregister_8_o4, bitregister_8_o5, bitregister_8_o6, bitregister_8_o7, bitregister_9_o0,
       bitregister_9_o1, bitregister_9_o2, bitregister_9_o3, bitregister_9_o4, bitregister_9_o5,
       bitregister_9_o6, bitregister_9_o7, bitregister_10_o0, bitregister_10_o1, bitregister_10_o2,
       bitregister_10_o3, bitregister_10_o4, bitregister_10_o5, bitregister_10_o6, bitregister_10_o7,
       bitregister_11_o0, bitregister_11_o1, bitregister_11_o2, bitregister_11_o3, bitregister_11_o4,
       bitregister_11_o5, bitregister_11_o6, bitregister_11_o7, bitregister_12_o0, bitregister_12_o1,
       bitregister_12_o2, bitregister_12_o3, bitregister_12_o4, bitregister_12_o5, bitregister_12_o6,
       bitregister_12_o7, bitregister_13_o0, bitregister_13_o1, bitregister_13_o2, bitregister_13_o3,
       bitregister_13_o4, bitregister_13_o5, bitregister_13_o6, bitregister_13_o7, bitregister_14_o0,
       bitregister_14_o1, bitregister_14_o2, bitregister_14_o3, bitregister_14_o4, bitregister_14_o5,
       bitregister_14_o6, bitregister_14_o7, bitregister_15_o0, bitregister_15_o1, bitregister_15_o2,
       bitregister_15_o3, bitregister_15_o4, bitregister_15_o5, bitregister_15_o6, bitregister_15_o7,
       bitregister_16_o0, bitregister_16_o1, bitregister_16_o2, bitregister_16_o3, bitregister_16_o4,
       bitregister_16_o5, bitregister_16_o6, bitregister_16_o7;
  wire [7:0] controlled_buffer_2_out;

  Adress_decoder_4bts adress_decoder_4bts_1 (
    .A4(A4), .A3(A3), .A2(A2), .A1(A1), .en(Enable), .DF(adress_decoder_4bts_1_df),
    .DE(adress_decoder_4bts_1_de), .DD(adress_decoder_4bts_1_dd), .DC(adress_decoder_4bts_1_dc),
    .DB(adress_decoder_4bts_1_db), .DA(adress_decoder_4bts_1_da), .D9(adress_decoder_4bts_1_d9),
    .D8(adress_decoder_4bts_1_d8), .D7(adress_decoder_4bts_1_d7), .D6(adress_decoder_4bts_1_d6),
    .D5(adress_decoder_4bts_1_d5), .D4(adress_decoder_4bts_1_d4), .D3(adress_decoder_4bts_1_d3),
    .D2(adress_decoder_4bts_1_d2), .D1(adress_decoder_4bts_1_d1), .D0(adress_decoder_4bts_1_d0));
  assign Q = Read ? {S7, S6, S5, S4, S3, S2, S1, S0} : 8'bz;  // Controlled_Buffer controlled_buffer_1
  DotMatrix #(.dotshape("circle"), .inputtype("row"), .matrixcols(1), .matrixrows(8)) dotmatrix_1 (
    .row0(bitregister_1_o0), .row1(bitregister_1_o1), .row2(bitregister_1_o2), .row3(bitregister_1_o3),
    .row4(bitregister_1_o4), .row5(bitregister_1_o5), .row6(bitregister_1_o6), .row7(bitregister_1_o7));
  BitRegister bitregister_1 (
    .reset(clear), .Load(and_1_out), .CLK(CLK), .reg_in(controlled_buffer_2_out),
    .reg_out_en(adress_decoder_4bts_1_df), .reg_out({S7, S6, S5, S4, S3, S2, S1, S0}), .O5(bitregister_1_o5),
    .O6(bitregister_1_o6), .O7(bitregister_1_o7), .O0(bitregister_1_o0), .O1(bitregister_1_o1),
    .O2(bitregister_1_o2), .O3(bitregister_1_o3), .O4(bitregister_1_o4));
  and and_1 (and_1_out, adress_decoder_4bts_1_df, Write);
  DotMatrix #(.dotshape("circle"), .inputtype("row"), .matrixcols(1), .matrixrows(8)) dotmatrix_2 (
    .row0(bitregister_2_o0), .row1(bitregister_2_o1), .row2(bitregister_2_o2), .row3(bitregister_2_o3),
    .row4(bitregister_2_o4), .row5(bitregister_2_o5), .row6(bitregister_2_o6), .row7(bitregister_2_o7));
  BitRegister bitregister_2 (
    .reset(clear), .Load(and_2_out), .CLK(CLK), .reg_in(controlled_buffer_2_out),
    .reg_out_en(adress_decoder_4bts_1_de), .reg_out({S7, S6, S5, S4, S3, S2, S1, S0}), .O5(bitregister_2_o5),
    .O6(bitregister_2_o6), .O7(bitregister_2_o7), .O0(bitregister_2_o0), .O1(bitregister_2_o1),
    .O2(bitregister_2_o2), .O3(bitregister_2_o3), .O4(bitregister_2_o4));
  and and_2 (and_2_out, adress_decoder_4bts_1_de, Write);
  DotMatrix #(.dotshape("circle"), .inputtype("row"), .matrixcols(1), .matrixrows(8)) dotmatrix_3 (
    .row0(bitregister_3_o0), .row1(bitregister_3_o1), .row2(bitregister_3_o2), .row3(bitregister_3_o3),
    .row4(bitregister_3_o4), .row5(bitregister_3_o5), .row6(bitregister_3_o6), .row7(bitregister_3_o7));
  BitRegister bitregister_3 (
    .reset(clear), .Load(and_3_out), .CLK(CLK), .reg_in(controlled_buffer_2_out),
    .reg_out_en(adress_decoder_4bts_1_dd), .reg_out({S7, S6, S5, S4, S3, S2, S1, S0}), .O5(bitregister_3_o5),
    .O6(bitregister_3_o6), .O7(bitregister_3_o7), .O0(bitregister_3_o0), .O1(bitregister_3_o1),
    .O2(bitregister_3_o2), .O3(bitregister_3_o3), .O4(bitregister_3_o4));
  and and_3 (and_3_out, adress_decoder_4bts_1_dd, Write);
  DotMatrix #(.dotshape("circle"), .inputtype("row"), .matrixcols(1), .matrixrows(8)) dotmatrix_4 (
    .row0(bitregister_4_o0), .row1(bitregister_4_o1), .row2(bitregister_4_o2), .row3(bitregister_4_o3),
    .row4(bitregister_4_o4), .row5(bitregister_4_o5), .row6(bitregister_4_o6), .row7(bitregister_4_o7));
  BitRegister bitregister_4 (
    .reset(clear), .Load(and_4_out), .CLK(CLK), .reg_in(controlled_buffer_2_out),
    .reg_out_en(adress_decoder_4bts_1_dc), .reg_out({S7, S6, S5, S4, S3, S2, S1, S0}), .O5(bitregister_4_o5),
    .O6(bitregister_4_o6), .O7(bitregister_4_o7), .O0(bitregister_4_o0), .O1(bitregister_4_o1),
    .O2(bitregister_4_o2), .O3(bitregister_4_o3), .O4(bitregister_4_o4));
  and and_4 (and_4_out, adress_decoder_4bts_1_dc, Write);
  DotMatrix #(.dotshape("circle"), .inputtype("row"), .matrixcols(1), .matrixrows(8)) dotmatrix_5 (
    .row0(bitregister_5_o0), .row1(bitregister_5_o1), .row2(bitregister_5_o2), .row3(bitregister_5_o3),
    .row4(bitregister_5_o4), .row5(bitregister_5_o5), .row6(bitregister_5_o6), .row7(bitregister_5_o7));
  BitRegister bitregister_5 (
    .reset(clear), .Load(and_5_out), .CLK(CLK), .reg_in(controlled_buffer_2_out),
    .reg_out_en(adress_decoder_4bts_1_db), .reg_out({S7, S6, S5, S4, S3, S2, S1, S0}), .O5(bitregister_5_o5),
    .O6(bitregister_5_o6), .O7(bitregister_5_o7), .O0(bitregister_5_o0), .O1(bitregister_5_o1),
    .O2(bitregister_5_o2), .O3(bitregister_5_o3), .O4(bitregister_5_o4));
  and and_5 (and_5_out, adress_decoder_4bts_1_db, Write);
  DotMatrix #(.dotshape("circle"), .inputtype("row"), .matrixcols(1), .matrixrows(8)) dotmatrix_6 (
    .row0(bitregister_6_o0), .row1(bitregister_6_o1), .row2(bitregister_6_o2), .row3(bitregister_6_o3),
    .row4(bitregister_6_o4), .row5(bitregister_6_o5), .row6(bitregister_6_o6), .row7(bitregister_6_o7));
  BitRegister bitregister_6 (
    .reset(clear), .Load(and_6_out), .CLK(CLK), .reg_in(controlled_buffer_2_out),
    .reg_out_en(adress_decoder_4bts_1_da), .reg_out({S7, S6, S5, S4, S3, S2, S1, S0}), .O5(bitregister_6_o5),
    .O6(bitregister_6_o6), .O7(bitregister_6_o7), .O0(bitregister_6_o0), .O1(bitregister_6_o1),
    .O2(bitregister_6_o2), .O3(bitregister_6_o3), .O4(bitregister_6_o4));
  and and_6 (and_6_out, adress_decoder_4bts_1_da, Write);
  DotMatrix #(.dotshape("circle"), .inputtype("row"), .matrixcols(1), .matrixrows(8)) dotmatrix_7 (
    .row0(bitregister_7_o0), .row1(bitregister_7_o1), .row2(bitregister_7_o2), .row3(bitregister_7_o3),
    .row4(bitregister_7_o4), .row5(bitregister_7_o5), .row6(bitregister_7_o6), .row7(bitregister_7_o7));
  BitRegister bitregister_7 (
    .reset(clear), .Load(and_7_out), .CLK(CLK), .reg_in(controlled_buffer_2_out),
    .reg_out_en(adress_decoder_4bts_1_d9), .reg_out({S7, S6, S5, S4, S3, S2, S1, S0}), .O5(bitregister_7_o5),
    .O6(bitregister_7_o6), .O7(bitregister_7_o7), .O0(bitregister_7_o0), .O1(bitregister_7_o1),
    .O2(bitregister_7_o2), .O3(bitregister_7_o3), .O4(bitregister_7_o4));
  and and_7 (and_7_out, adress_decoder_4bts_1_d9, Write);
  DotMatrix #(.dotshape("circle"), .inputtype("row"), .matrixcols(1), .matrixrows(8)) dotmatrix_8 (
    .row0(bitregister_8_o0), .row1(bitregister_8_o1), .row2(bitregister_8_o2), .row3(bitregister_8_o3),
    .row4(bitregister_8_o4), .row5(bitregister_8_o5), .row6(bitregister_8_o6), .row7(bitregister_8_o7));
  BitRegister bitregister_8 (
    .reset(clear), .Load(and_8_out), .CLK(CLK), .reg_in(controlled_buffer_2_out),
    .reg_out_en(adress_decoder_4bts_1_d8), .reg_out({S7, S6, S5, S4, S3, S2, S1, S0}), .O5(bitregister_8_o5),
    .O6(bitregister_8_o6), .O7(bitregister_8_o7), .O0(bitregister_8_o0), .O1(bitregister_8_o1),
    .O2(bitregister_8_o2), .O3(bitregister_8_o3), .O4(bitregister_8_o4));
  and and_8 (and_8_out, adress_decoder_4bts_1_d8, Write);
  assign controlled_buffer_2_out = Write ? D : 8'bz;  // Controlled_Buffer controlled_buffer_2
  DotMatrix #(.dotshape("circle"), .inputtype("row"), .matrixcols(1), .matrixrows(8)) dotmatrix_9 (
    .row0(bitregister_9_o0), .row1(bitregister_9_o1), .row2(bitregister_9_o2), .row3(bitregister_9_o3),
    .row4(bitregister_9_o4), .row5(bitregister_9_o5), .row6(bitregister_9_o6), .row7(bitregister_9_o7));
  BitRegister bitregister_9 (
    .reset(clear), .Load(and_9_out), .CLK(CLK), .reg_in(controlled_buffer_2_out),
    .reg_out_en(adress_decoder_4bts_1_d0), .reg_out({S7, S6, S5, S4, S3, S2, S1, S0}), .O5(bitregister_9_o5),
    .O6(bitregister_9_o6), .O7(bitregister_9_o7), .O0(bitregister_9_o0), .O1(bitregister_9_o1),
    .O2(bitregister_9_o2), .O3(bitregister_9_o3), .O4(bitregister_9_o4));
  and and_9 (and_9_out, adress_decoder_4bts_1_d0, Write);
  DotMatrix #(.dotshape("circle"), .inputtype("row"), .matrixcols(1), .matrixrows(8)) dotmatrix_10 (
    .row0(bitregister_10_o0), .row1(bitregister_10_o1), .row2(bitregister_10_o2), .row3(bitregister_10_o3),
    .row4(bitregister_10_o4), .row5(bitregister_10_o5), .row6(bitregister_10_o6), .row7(bitregister_10_o7));
  BitRegister bitregister_10 (
    .reset(clear), .Load(and_10_out), .CLK(CLK), .reg_in(controlled_buffer_2_out),
    .reg_out_en(adress_decoder_4bts_1_d1), .reg_out({S7, S6, S5, S4, S3, S2, S1, S0}),
    .O5(bitregister_10_o5), .O6(bitregister_10_o6), .O7(bitregister_10_o7), .O0(bitregister_10_o0),
    .O1(bitregister_10_o1), .O2(bitregister_10_o2), .O3(bitregister_10_o3), .O4(bitregister_10_o4));
  and and_10 (and_10_out, adress_decoder_4bts_1_d1, Write);
  DotMatrix #(.dotshape("circle"), .inputtype("row"), .matrixcols(1), .matrixrows(8)) dotmatrix_11 (
    .row0(bitregister_11_o0), .row1(bitregister_11_o1), .row2(bitregister_11_o2), .row3(bitregister_11_o3),
    .row4(bitregister_11_o4), .row5(bitregister_11_o5), .row6(bitregister_11_o6), .row7(bitregister_11_o7));
  BitRegister bitregister_11 (
    .reset(clear), .Load(and_11_out), .CLK(CLK), .reg_in(controlled_buffer_2_out),
    .reg_out_en(adress_decoder_4bts_1_d2), .reg_out({S7, S6, S5, S4, S3, S2, S1, S0}),
    .O5(bitregister_11_o5), .O6(bitregister_11_o6), .O7(bitregister_11_o7), .O0(bitregister_11_o0),
    .O1(bitregister_11_o1), .O2(bitregister_11_o2), .O3(bitregister_11_o3), .O4(bitregister_11_o4));
  and and_11 (and_11_out, adress_decoder_4bts_1_d2, Write);
  DotMatrix #(.dotshape("circle"), .inputtype("row"), .matrixcols(1), .matrixrows(8)) dotmatrix_12 (
    .row0(bitregister_12_o0), .row1(bitregister_12_o1), .row2(bitregister_12_o2), .row3(bitregister_12_o3),
    .row4(bitregister_12_o4), .row5(bitregister_12_o5), .row6(bitregister_12_o6), .row7(bitregister_12_o7));
  BitRegister bitregister_12 (
    .reset(clear), .Load(and_12_out), .CLK(CLK), .reg_in(controlled_buffer_2_out),
    .reg_out_en(adress_decoder_4bts_1_d3), .reg_out({S7, S6, S5, S4, S3, S2, S1, S0}),
    .O5(bitregister_12_o5), .O6(bitregister_12_o6), .O7(bitregister_12_o7), .O0(bitregister_12_o0),
    .O1(bitregister_12_o1), .O2(bitregister_12_o2), .O3(bitregister_12_o3), .O4(bitregister_12_o4));
  and and_12 (and_12_out, adress_decoder_4bts_1_d3, Write);
  DotMatrix #(.dotshape("circle"), .inputtype("row"), .matrixcols(1), .matrixrows(8)) dotmatrix_13 (
    .row0(bitregister_13_o0), .row1(bitregister_13_o1), .row2(bitregister_13_o2), .row3(bitregister_13_o3),
    .row4(bitregister_13_o4), .row5(bitregister_13_o5), .row6(bitregister_13_o6), .row7(bitregister_13_o7));
  BitRegister bitregister_13 (
    .reset(clear), .Load(and_13_out), .CLK(CLK), .reg_in(controlled_buffer_2_out),
    .reg_out_en(adress_decoder_4bts_1_d4), .reg_out({S7, S6, S5, S4, S3, S2, S1, S0}),
    .O5(bitregister_13_o5), .O6(bitregister_13_o6), .O7(bitregister_13_o7), .O0(bitregister_13_o0),
    .O1(bitregister_13_o1), .O2(bitregister_13_o2), .O3(bitregister_13_o3), .O4(bitregister_13_o4));
  and and_13 (and_13_out, adress_decoder_4bts_1_d4, Write);
  DotMatrix #(.dotshape("circle"), .inputtype("row"), .matrixcols(1), .matrixrows(8)) dotmatrix_14 (
    .row0(bitregister_14_o0), .row1(bitregister_14_o1), .row2(bitregister_14_o2), .row3(bitregister_14_o3),
    .row4(bitregister_14_o4), .row5(bitregister_14_o5), .row6(bitregister_14_o6), .row7(bitregister_14_o7));
  BitRegister bitregister_14 (
    .reset(clear), .Load(and_14_out), .CLK(CLK), .reg_in(controlled_buffer_2_out),
    .reg_out_en(adress_decoder_4bts_1_d5), .reg_out({S7, S6, S5, S4, S3, S2, S1, S0}),
    .O5(bitregister_14_o5), .O6(bitregister_14_o6), .O7(bitregister_14_o7), .O0(bitregister_14_o0),
    .O1(bitregister_14_o1), .O2(bitregister_14_o2), .O3(bitregister_14_o3), .O4(bitregister_14_o4));
  and and_14 (and_14_out, adress_decoder_4bts_1_d5, Write);
  DotMatrix #(.dotshape("circle"), .inputtype("row"), .matrixcols(1), .matrixrows(8)) dotmatrix_15 (
    .row0(bitregister_15_o0), .row1(bitregister_15_o1), .row2(bitregister_15_o2), .row3(bitregister_15_o3),
    .row4(bitregister_15_o4), .row5(bitregister_15_o5), .row6(bitregister_15_o6), .row7(bitregister_15_o7));
  BitRegister bitregister_15 (
    .reset(clear), .Load(and_15_out), .CLK(CLK), .reg_in(controlled_buffer_2_out),
    .reg_out_en(adress_decoder_4bts_1_d6), .reg_out({S7, S6, S5, S4, S3, S2, S1, S0}),
    .O5(bitregister_15_o5), .O6(bitregister_15_o6), .O7(bitregister_15_o7), .O0(bitregister_15_o0),
    .O1(bitregister_15_o1), .O2(bitregister_15_o2), .O3(bitregister_15_o3), .O4(bitregister_15_o4));
  and and_15 (and_15_out, adress_decoder_4bts_1_d6, Write);
  DotMatrix #(.dotshape("circle"), .inputtype("row"), .matrixcols(1), .matrixrows(8)) dotmatrix_16 (
    .row0(bitregister_16_o0), .row1(bitregister_16_o1), .row2(bitregister_16_o2), .row3(bitregister_16_o3),
    .row4(bitregister_16_o4), .row5(bitregister_16_o5), .row6(bitregister_16_o6), .row7(bitregister_16_o7));
  BitRegister bitregister_16 (
    .reset(clear), .Load(and_16_out), .CLK(CLK), .reg_in(controlled_buffer_2_out),
    .reg_out_en(adress_decoder_4bts_1_d7), .reg_out({S7, S6, S5, S4, S3, S2, S1, S0}),
    .O5(bitregister_16_o5), .O6(bitregister_16_o6), .O7(bitregister_16_o7), .O0(bitregister_16_o0),
    .O1(bitregister_16_o1), .O2(bitregister_16_o2), .O3(bitregister_16_o3), .O4(bitregister_16_o4));
  and and_16 (and_16_out, adress_decoder_4bts_1_d7, Write);
endmodule

module SRAM_256_Bytes (
  input  [7:0] I,
  input  CLK,
  input  Write,
  input  A7,
  input  A6,
  input  Read,
  input  A5,
  input  A4,
  input  A3,
  input  A2,
  input  A1,
  input  A0,
  input  CLR,
  output S0,
  output S1,
  output S2,
  output [7:0] Q,
  output S3,
  output S4,
  output S5,
  output S6,
  output S7
);

  wire and_1_out, and_2_out, and_3_out, and_4_out, and_5_out, and_6_out, and_7_out, and_8_out, and_9_out,
       and_10_out, and_11_out, and_12_out, and_13_out, and_14_out, and_15_out, and_16_out, Decoder_4_bits_d0,
       Decoder_4_bits_d1, Decoder_4_bits_d2, Decoder_4_bits_d3, Decoder_4_bits_d4, Decoder_4_bits_d5,
       Decoder_4_bits_d6, Decoder_4_bits_d7, Decoder_4_bits_d8, Decoder_4_bits_d9, Decoder_4_bits_da,
       Decoder_4_bits_db, Decoder_4_bits_dc, Decoder_4_bits_dd, Decoder_4_bits_de, Decoder_4_bits_df,
       sram_16_bytes_1_s0, sram_16_bytes_1_s1, sram_16_bytes_1_s2, sram_16_bytes_1_s3, sram_16_bytes_1_s4,
       sram_16_bytes_1_s5, sram_16_bytes_1_s6, sram_16_bytes_1_s7, sram_16_bytes_2_s0, sram_16_bytes_2_s1,
       sram_16_bytes_2_s2, sram_16_bytes_2_s3, sram_16_bytes_2_s4, sram_16_bytes_2_s5, sram_16_bytes_2_s6,
       sram_16_bytes_2_s7, sram_16_bytes_3_s0, sram_16_bytes_3_s1, sram_16_bytes_3_s2, sram_16_bytes_3_s3,
       sram_16_bytes_3_s4, sram_16_bytes_3_s5, sram_16_bytes_3_s6, sram_16_bytes_3_s7, sram_16_bytes_4_s0,
       sram_16_bytes_4_s1, sram_16_bytes_4_s2, sram_16_bytes_4_s3, sram_16_bytes_4_s4, sram_16_bytes_4_s5,
       sram_16_bytes_4_s6, sram_16_bytes_4_s7, sram_16_bytes_5_s0, sram_16_bytes_5_s1, sram_16_bytes_5_s2,
       sram_16_bytes_5_s3, sram_16_bytes_5_s4, sram_16_bytes_5_s5, sram_16_bytes_5_s6, sram_16_bytes_5_s7,
       sram_16_bytes_6_s0, sram_16_bytes_6_s1, sram_16_bytes_6_s2, sram_16_bytes_6_s3, sram_16_bytes_6_s4,
       sram_16_bytes_6_s5, sram_16_bytes_6_s6, sram_16_bytes_6_s7, sram_16_bytes_7_s0, sram_16_bytes_7_s1,
       sram_16_bytes_7_s2, sram_16_bytes_7_s3, sram_16_bytes_7_s4, sram_16_bytes_7_s5, sram_16_bytes_7_s6,
       sram_16_bytes_7_s7, sram_16_bytes_8_s0, sram_16_bytes_8_s1, sram_16_bytes_8_s2, sram_16_bytes_8_s3,
       sram_16_bytes_8_s4, sram_16_bytes_8_s5, sram_16_bytes_8_s6, sram_16_bytes_8_s7, sram_16_bytes_9_s0,
       sram_16_bytes_9_s1, sram_16_bytes_9_s2, sram_16_bytes_9_s3, sram_16_bytes_9_s4, sram_16_bytes_9_s5,
       sram_16_bytes_9_s6, sram_16_bytes_9_s7, sram_16_bytes_10_s0, sram_16_bytes_10_s1, sram_16_bytes_10_s2,
       sram_16_bytes_10_s3, sram_16_bytes_10_s4, sram_16_bytes_10_s5, sram_16_bytes_10_s6,
       sram_16_bytes_10_s7, sram_16_bytes_11_s0, sram_16_bytes_11_s1, sram_16_bytes_11_s2,
       sram_16_bytes_11_s3, sram_16_bytes_11_s4, sram_16_bytes_11_s5, sram_16_bytes_11_s6,
       sram_16_bytes_11_s7, sram_16_bytes_12_s0, sram_16_bytes_12_s1, sram_16_bytes_12_s2,
       sram_16_bytes_12_s3, sram_16_bytes_12_s4, sram_16_bytes_12_s5, sram_16_bytes_12_s6,
       sram_16_bytes_12_s7, sram_16_bytes_13_s0, sram_16_bytes_13_s1, sram_16_bytes_13_s2,
       sram_16_bytes_13_s3, sram_16_bytes_13_s4, sram_16_bytes_13_s5, sram_16_bytes_13_s6,
       sram_16_bytes_13_s7, sram_16_bytes_14_s0, sram_16_bytes_14_s1, sram_16_bytes_14_s2,
       sram_16_bytes_14_s3, sram_16_bytes_14_s4, sram_16_bytes_14_s5, sram_16_bytes_14_s6,
       sram_16_bytes_14_s7, sram_16_bytes_15_s0, sram_16_bytes_15_s1, sram_16_bytes_15_s2,
       sram_16_bytes_15_s3, sram_16_bytes_15_s4, sram_16_bytes_15_s5, sram_16_bytes_15_s6,
       sram_16_bytes_15_s7, sram_16_bytes_16_s0, sram_16_bytes_16_s1, sram_16_bytes_16_s2,
       sram_16_bytes_16_s3, sram_16_bytes_16_s4, sram_16_bytes_16_s5, sram_16_bytes_16_s6,
       sram_16_bytes_16_s7;
  wire [7:0] controlled_buffer_1_out;

  Adress_decoder_4bts Decoder_4_bits (
    .A4(A7), .A3(A6), .A2(A5), .A1(A4), .en(1'b1), .DF(Decoder_4_bits_df), .DE(Decoder_4_bits_de),
    .DD(Decoder_4_bits_dd), .DC(Decoder_4_bits_dc), .DB(Decoder_4_bits_db), .DA(Decoder_4_bits_da),
    .D9(Decoder_4_bits_d9), .D8(Decoder_4_bits_d8), .D7(Decoder_4_bits_d7), .D6(Decoder_4_bits_d6),
    .D5(Decoder_4_bits_d5), .D4(Decoder_4_bits_d4), .D3(Decoder_4_bits_d3), .D2(Decoder_4_bits_d2),
    .D1(Decoder_4_bits_d1), .D0(Decoder_4_bits_d0));
  and and_1 (and_1_out, Write, Decoder_4_bits_df);
  and and_2 (and_2_out, Write, Decoder_4_bits_de);
  and and_3 (and_3_out, Write, Decoder_4_bits_dd);
  and and_4 (and_4_out, Write, Decoder_4_bits_dc);
  and and_5 (and_5_out, Write, Decoder_4_bits_db);
  and and_6 (and_6_out, Write, Decoder_4_bits_da);
  and and_7 (and_7_out, Write, Decoder_4_bits_d9);
  and and_8 (and_8_out, Write, Decoder_4_bits_d8);
  SRAM_16_Bytes sram_16_bytes_1 (
    .Read(Decoder_4_bits_df), .A4(A3), .A3(A2), .A2(A1), .A1(A0), .Enable(1'b1), .Write(and_1_out),
    .clear(CLR), .CLK(CLK), .D(controlled_buffer_1_out), .Q({S7, S6, S5, S4, S3, S2, S1, S0}),
    .S7(sram_16_bytes_1_s7), .S6(sram_16_bytes_1_s6), .S5(sram_16_bytes_1_s5), .S4(sram_16_bytes_1_s4),
    .S3(sram_16_bytes_1_s3), .S2(sram_16_bytes_1_s2), .S1(sram_16_bytes_1_s1), .S0(sram_16_bytes_1_s0));
  DotMatrix #(.dotshape("circle"), .inputtype("row"), .matrixcols(1), .matrixrows(8)) dotmatrix_1 (
    .row0(sram_16_bytes_1_s7), .row1(sram_16_bytes_1_s6), .row2(sram_16_bytes_1_s5),
    .row3(sram_16_bytes_1_s4), .row4(sram_16_bytes_1_s3), .row5(sram_16_bytes_1_s2),
    .row6(sram_16_bytes_1_s1), .row7(sram_16_bytes_1_s0));
  SRAM_16_Bytes sram_16_bytes_2 (
    .Read(Decoder_4_bits_de), .A4(A3), .A3(A2), .A2(A1), .A1(A0), .Enable(1'b1), .Write(and_2_out),
    .clear(CLR), .CLK(CLK), .D(controlled_buffer_1_out), .Q({S7, S6, S5, S4, S3, S2, S1, S0}),
    .S7(sram_16_bytes_2_s7), .S6(sram_16_bytes_2_s6), .S5(sram_16_bytes_2_s5), .S4(sram_16_bytes_2_s4),
    .S3(sram_16_bytes_2_s3), .S2(sram_16_bytes_2_s2), .S1(sram_16_bytes_2_s1), .S0(sram_16_bytes_2_s0));
  DotMatrix #(.dotshape("circle"), .inputtype("row"), .matrixcols(1), .matrixrows(8)) dotmatrix_2 (
    .row0(sram_16_bytes_2_s7), .row1(sram_16_bytes_2_s6), .row2(sram_16_bytes_2_s5),
    .row3(sram_16_bytes_2_s4), .row4(sram_16_bytes_2_s3), .row5(sram_16_bytes_2_s2),
    .row6(sram_16_bytes_2_s1), .row7(sram_16_bytes_2_s0));
  SRAM_16_Bytes sram_16_bytes_3 (
    .Read(Decoder_4_bits_dd), .A4(A3), .A3(A2), .A2(A1), .A1(A0), .Enable(1'b1), .Write(and_3_out),
    .clear(CLR), .CLK(CLK), .D(controlled_buffer_1_out), .Q({S7, S6, S5, S4, S3, S2, S1, S0}),
    .S7(sram_16_bytes_3_s7), .S6(sram_16_bytes_3_s6), .S5(sram_16_bytes_3_s5), .S4(sram_16_bytes_3_s4),
    .S3(sram_16_bytes_3_s3), .S2(sram_16_bytes_3_s2), .S1(sram_16_bytes_3_s1), .S0(sram_16_bytes_3_s0));
  DotMatrix #(.dotshape("circle"), .inputtype("row"), .matrixcols(1), .matrixrows(8)) dotmatrix_3 (
    .row0(sram_16_bytes_3_s7), .row1(sram_16_bytes_3_s6), .row2(sram_16_bytes_3_s5),
    .row3(sram_16_bytes_3_s4), .row4(sram_16_bytes_3_s3), .row5(sram_16_bytes_3_s2),
    .row6(sram_16_bytes_3_s1), .row7(sram_16_bytes_3_s0));
  SRAM_16_Bytes sram_16_bytes_4 (
    .Read(Decoder_4_bits_dc), .A4(A3), .A3(A2), .A2(A1), .A1(A0), .Enable(1'b1), .Write(and_4_out),
    .clear(CLR), .CLK(CLK), .D(controlled_buffer_1_out), .Q({S7, S6, S5, S4, S3, S2, S1, S0}),
    .S7(sram_16_bytes_4_s7), .S6(sram_16_bytes_4_s6), .S5(sram_16_bytes_4_s5), .S4(sram_16_bytes_4_s4),
    .S3(sram_16_bytes_4_s3), .S2(sram_16_bytes_4_s2), .S1(sram_16_bytes_4_s1), .S0(sram_16_bytes_4_s0));
  DotMatrix #(.dotshape("circle"), .inputtype("row"), .matrixcols(1), .matrixrows(8)) dotmatrix_4 (
    .row0(sram_16_bytes_4_s7), .row1(sram_16_bytes_4_s6), .row2(sram_16_bytes_4_s5),
    .row3(sram_16_bytes_4_s4), .row4(sram_16_bytes_4_s3), .row5(sram_16_bytes_4_s2),
    .row6(sram_16_bytes_4_s1), .row7(sram_16_bytes_4_s0));
  SRAM_16_Bytes sram_16_bytes_5 (
    .Read(Decoder_4_bits_db), .A4(A3), .A3(A2), .A2(A1), .A1(A0), .Enable(1'b1), .Write(and_5_out),
    .clear(CLR), .CLK(CLK), .D(controlled_buffer_1_out), .Q({S7, S6, S5, S4, S3, S2, S1, S0}),
    .S7(sram_16_bytes_5_s7), .S6(sram_16_bytes_5_s6), .S5(sram_16_bytes_5_s5), .S4(sram_16_bytes_5_s4),
    .S3(sram_16_bytes_5_s3), .S2(sram_16_bytes_5_s2), .S1(sram_16_bytes_5_s1), .S0(sram_16_bytes_5_s0));
  DotMatrix #(.dotshape("circle"), .inputtype("row"), .matrixcols(1), .matrixrows(8)) dotmatrix_5 (
    .row0(sram_16_bytes_5_s7), .row1(sram_16_bytes_5_s6), .row2(sram_16_bytes_5_s5),
    .row3(sram_16_bytes_5_s4), .row4(sram_16_bytes_5_s3), .row5(sram_16_bytes_5_s2),
    .row6(sram_16_bytes_5_s1), .row7(sram_16_bytes_5_s0));
  SRAM_16_Bytes sram_16_bytes_6 (
    .Read(Decoder_4_bits_da), .A4(A3), .A3(A2), .A2(A1), .A1(A0), .Enable(1'b1), .Write(and_6_out),
    .clear(CLR), .CLK(CLK), .D(controlled_buffer_1_out), .Q({S7, S6, S5, S4, S3, S2, S1, S0}),
    .S7(sram_16_bytes_6_s7), .S6(sram_16_bytes_6_s6), .S5(sram_16_bytes_6_s5), .S4(sram_16_bytes_6_s4),
    .S3(sram_16_bytes_6_s3), .S2(sram_16_bytes_6_s2), .S1(sram_16_bytes_6_s1), .S0(sram_16_bytes_6_s0));
  DotMatrix #(.dotshape("circle"), .inputtype("row"), .matrixcols(1), .matrixrows(8)) dotmatrix_6 (
    .row0(sram_16_bytes_6_s7), .row1(sram_16_bytes_6_s6), .row2(sram_16_bytes_6_s5),
    .row3(sram_16_bytes_6_s4), .row4(sram_16_bytes_6_s3), .row5(sram_16_bytes_6_s2),
    .row6(sram_16_bytes_6_s1), .row7(sram_16_bytes_6_s0));
  SRAM_16_Bytes sram_16_bytes_7 (
    .Read(Decoder_4_bits_d9), .A4(A3), .A3(A2), .A2(A1), .A1(A0), .Enable(1'b1), .Write(and_7_out),
    .clear(CLR), .CLK(CLK), .D(controlled_buffer_1_out), .Q({S7, S6, S5, S4, S3, S2, S1, S0}),
    .S7(sram_16_bytes_7_s7), .S6(sram_16_bytes_7_s6), .S5(sram_16_bytes_7_s5), .S4(sram_16_bytes_7_s4),
    .S3(sram_16_bytes_7_s3), .S2(sram_16_bytes_7_s2), .S1(sram_16_bytes_7_s1), .S0(sram_16_bytes_7_s0));
  DotMatrix #(.dotshape("circle"), .inputtype("row"), .matrixcols(1), .matrixrows(8)) dotmatrix_7 (
    .row0(sram_16_bytes_7_s7), .row1(sram_16_bytes_7_s6), .row2(sram_16_bytes_7_s5),
    .row3(sram_16_bytes_7_s4), .row4(sram_16_bytes_7_s3), .row5(sram_16_bytes_7_s2),
    .row6(sram_16_bytes_7_s1), .row7(sram_16_bytes_7_s0));
  SRAM_16_Bytes sram_16_bytes_8 (
    .Read(Decoder_4_bits_d8), .A4(A3), .A3(A2), .A2(A1), .A1(A0), .Enable(1'b1), .Write(and_8_out),
    .clear(CLR), .CLK(CLK), .D(controlled_buffer_1_out), .Q({S7, S6, S5, S4, S3, S2, S1, S0}),
    .S7(sram_16_bytes_8_s7), .S6(sram_16_bytes_8_s6), .S5(sram_16_bytes_8_s5), .S4(sram_16_bytes_8_s4),
    .S3(sram_16_bytes_8_s3), .S2(sram_16_bytes_8_s2), .S1(sram_16_bytes_8_s1), .S0(sram_16_bytes_8_s0));
  DotMatrix #(.dotshape("circle"), .inputtype("row"), .matrixcols(1), .matrixrows(8)) dotmatrix_8 (
    .row0(sram_16_bytes_8_s7), .row1(sram_16_bytes_8_s6), .row2(sram_16_bytes_8_s5),
    .row3(sram_16_bytes_8_s4), .row4(sram_16_bytes_8_s3), .row5(sram_16_bytes_8_s2),
    .row6(sram_16_bytes_8_s1), .row7(sram_16_bytes_8_s0));
  assign controlled_buffer_1_out = Write ? I : 8'bz;  // Controlled_Buffer controlled_buffer_1
  and and_9 (and_9_out, Write, Decoder_4_bits_d0);
  and and_10 (and_10_out, Write, Decoder_4_bits_d1);
  and and_11 (and_11_out, Write, Decoder_4_bits_d2);
  and and_12 (and_12_out, Write, Decoder_4_bits_d3);
  and and_13 (and_13_out, Write, Decoder_4_bits_d4);
  and and_14 (and_14_out, Write, Decoder_4_bits_d5);
  and and_15 (and_15_out, Write, Decoder_4_bits_d6);
  and and_16 (and_16_out, Write, Decoder_4_bits_d7);
  assign Q = Read ? {S7, S6, S5, S4, S3, S2, S1, S0} : 8'bz;  // Controlled_Buffer controlled_buffer_2
  SRAM_16_Bytes sram_16_bytes_9 (
    .Read(Decoder_4_bits_d0), .A4(A3), .A3(A2), .A2(A1), .A1(A0), .Enable(1'b1), .Write(and_9_out),
    .clear(CLR), .CLK(CLK), .D(controlled_buffer_1_out), .Q({S7, S6, S5, S4, S3, S2, S1, S0}),
    .S7(sram_16_bytes_9_s7), .S6(sram_16_bytes_9_s6), .S5(sram_16_bytes_9_s5), .S4(sram_16_bytes_9_s4),
    .S3(sram_16_bytes_9_s3), .S2(sram_16_bytes_9_s2), .S1(sram_16_bytes_9_s1), .S0(sram_16_bytes_9_s0));
  DotMatrix #(.dotshape("circle"), .inputtype("row"), .matrixcols(1), .matrixrows(8)) dotmatrix_9 (
    .row0(sram_16_bytes_9_s7), .row1(sram_16_bytes_9_s6), .row2(sram_16_bytes_9_s5),
    .row3(sram_16_bytes_9_s4), .row4(sram_16_bytes_9_s3), .row5(sram_16_bytes_9_s2),
    .row6(sram_16_bytes_9_s1), .row7(sram_16_bytes_9_s0));
  SRAM_16_Bytes sram_16_bytes_10 (
    .Read(Decoder_4_bits_d1), .A4(A3), .A3(A2), .A2(A1), .A1(A0), .Enable(1'b1), .Write(and_10_out),
    .clear(CLR), .CLK(CLK), .D(controlled_buffer_1_out), .Q({S7, S6, S5, S4, S3, S2, S1, S0}),
    .S7(sram_16_bytes_10_s7), .S6(sram_16_bytes_10_s6), .S5(sram_16_bytes_10_s5), .S4(sram_16_bytes_10_s4),
    .S3(sram_16_bytes_10_s3), .S2(sram_16_bytes_10_s2), .S1(sram_16_bytes_10_s1), .S0(sram_16_bytes_10_s0));
  DotMatrix #(.dotshape("circle"), .inputtype("row"), .matrixcols(1), .matrixrows(8)) dotmatrix_10 (
    .row0(sram_16_bytes_10_s7), .row1(sram_16_bytes_10_s6), .row2(sram_16_bytes_10_s5),
    .row3(sram_16_bytes_10_s4), .row4(sram_16_bytes_10_s3), .row5(sram_16_bytes_10_s2),
    .row6(sram_16_bytes_10_s1), .row7(sram_16_bytes_10_s0));
  SRAM_16_Bytes sram_16_bytes_11 (
    .Read(Decoder_4_bits_d2), .A4(A3), .A3(A2), .A2(A1), .A1(A0), .Enable(1'b1), .Write(and_11_out),
    .clear(CLR), .CLK(CLK), .D(controlled_buffer_1_out), .Q({S7, S6, S5, S4, S3, S2, S1, S0}),
    .S7(sram_16_bytes_11_s7), .S6(sram_16_bytes_11_s6), .S5(sram_16_bytes_11_s5), .S4(sram_16_bytes_11_s4),
    .S3(sram_16_bytes_11_s3), .S2(sram_16_bytes_11_s2), .S1(sram_16_bytes_11_s1), .S0(sram_16_bytes_11_s0));
  DotMatrix #(.dotshape("circle"), .inputtype("row"), .matrixcols(1), .matrixrows(8)) dotmatrix_11 (
    .row0(sram_16_bytes_11_s7), .row1(sram_16_bytes_11_s6), .row2(sram_16_bytes_11_s5),
    .row3(sram_16_bytes_11_s4), .row4(sram_16_bytes_11_s3), .row5(sram_16_bytes_11_s2),
    .row6(sram_16_bytes_11_s1), .row7(sram_16_bytes_11_s0));
  SRAM_16_Bytes sram_16_bytes_12 (
    .Read(Decoder_4_bits_d3), .A4(A3), .A3(A2), .A2(A1), .A1(A0), .Enable(1'b1), .Write(and_12_out),
    .clear(CLR), .CLK(CLK), .D(controlled_buffer_1_out), .Q({S7, S6, S5, S4, S3, S2, S1, S0}),
    .S7(sram_16_bytes_12_s7), .S6(sram_16_bytes_12_s6), .S5(sram_16_bytes_12_s5), .S4(sram_16_bytes_12_s4),
    .S3(sram_16_bytes_12_s3), .S2(sram_16_bytes_12_s2), .S1(sram_16_bytes_12_s1), .S0(sram_16_bytes_12_s0));
  DotMatrix #(.dotshape("circle"), .inputtype("row"), .matrixcols(1), .matrixrows(8)) dotmatrix_12 (
    .row0(sram_16_bytes_12_s7), .row1(sram_16_bytes_12_s6), .row2(sram_16_bytes_12_s5),
    .row3(sram_16_bytes_12_s4), .row4(sram_16_bytes_12_s3), .row5(sram_16_bytes_12_s2),
    .row6(sram_16_bytes_12_s1), .row7(sram_16_bytes_12_s0));
  SRAM_16_Bytes sram_16_bytes_13 (
    .Read(Decoder_4_bits_d4), .A4(A3), .A3(A2), .A2(A1), .A1(A0), .Enable(1'b1), .Write(and_13_out),
    .clear(CLR), .CLK(CLK), .D(controlled_buffer_1_out), .Q({S7, S6, S5, S4, S3, S2, S1, S0}),
    .S7(sram_16_bytes_13_s7), .S6(sram_16_bytes_13_s6), .S5(sram_16_bytes_13_s5), .S4(sram_16_bytes_13_s4),
    .S3(sram_16_bytes_13_s3), .S2(sram_16_bytes_13_s2), .S1(sram_16_bytes_13_s1), .S0(sram_16_bytes_13_s0));
  DotMatrix #(.dotshape("circle"), .inputtype("row"), .matrixcols(1), .matrixrows(8)) dotmatrix_13 (
    .row0(sram_16_bytes_13_s7), .row1(sram_16_bytes_13_s6), .row2(sram_16_bytes_13_s5),
    .row3(sram_16_bytes_13_s4), .row4(sram_16_bytes_13_s3), .row5(sram_16_bytes_13_s2),
    .row6(sram_16_bytes_13_s1), .row7(sram_16_bytes_13_s0));
  SRAM_16_Bytes sram_16_bytes_14 (
    .Read(Decoder_4_bits_d5), .A4(A3), .A3(A2), .A2(A1), .A1(A0), .Enable(1'b1), .Write(and_14_out),
    .clear(CLR), .CLK(CLK), .D(controlled_buffer_1_out), .Q({S7, S6, S5, S4, S3, S2, S1, S0}),
    .S7(sram_16_bytes_14_s7), .S6(sram_16_bytes_14_s6), .S5(sram_16_bytes_14_s5), .S4(sram_16_bytes_14_s4),
    .S3(sram_16_bytes_14_s3), .S2(sram_16_bytes_14_s2), .S1(sram_16_bytes_14_s1), .S0(sram_16_bytes_14_s0));
  DotMatrix #(.dotshape("circle"), .inputtype("row"), .matrixcols(1), .matrixrows(8)) dotmatrix_14 (
    .row0(sram_16_bytes_14_s7), .row1(sram_16_bytes_14_s6), .row2(sram_16_bytes_14_s5),
    .row3(sram_16_bytes_14_s4), .row4(sram_16_bytes_14_s3), .row5(sram_16_bytes_14_s2),
    .row6(sram_16_bytes_14_s1), .row7(sram_16_bytes_14_s0));
  SRAM_16_Bytes sram_16_bytes_15 (
    .Read(Decoder_4_bits_d6), .A4(A3), .A3(A2), .A2(A1), .A1(A0), .Enable(1'b1), .Write(and_15_out),
    .clear(CLR), .CLK(CLK), .D(controlled_buffer_1_out), .Q({S7, S6, S5, S4, S3, S2, S1, S0}),
    .S7(sram_16_bytes_15_s7), .S6(sram_16_bytes_15_s6), .S5(sram_16_bytes_15_s5), .S4(sram_16_bytes_15_s4),
    .S3(sram_16_bytes_15_s3), .S2(sram_16_bytes_15_s2), .S1(sram_16_bytes_15_s1), .S0(sram_16_bytes_15_s0));
  DotMatrix #(.dotshape("circle"), .inputtype("row"), .matrixcols(1), .matrixrows(8)) dotmatrix_15 (
    .row0(sram_16_bytes_15_s7), .row1(sram_16_bytes_15_s6), .row2(sram_16_bytes_15_s5),
    .row3(sram_16_bytes_15_s4), .row4(sram_16_bytes_15_s3), .row5(sram_16_bytes_15_s2),
    .row6(sram_16_bytes_15_s1), .row7(sram_16_bytes_15_s0));
  SRAM_16_Bytes sram_16_bytes_16 (
    .Read(Decoder_4_bits_d7), .A4(A3), .A3(A2), .A2(A1), .A1(A0), .Enable(1'b1), .Write(and_16_out),
    .clear(CLR), .CLK(CLK), .D(controlled_buffer_1_out), .Q({S7, S6, S5, S4, S3, S2, S1, S0}),
    .S7(sram_16_bytes_16_s7), .S6(sram_16_bytes_16_s6), .S5(sram_16_bytes_16_s5), .S4(sram_16_bytes_16_s4),
    .S3(sram_16_bytes_16_s3), .S2(sram_16_bytes_16_s2), .S1(sram_16_bytes_16_s1), .S0(sram_16_bytes_16_s0));
  DotMatrix #(.dotshape("circle"), .inputtype("row"), .matrixcols(1), .matrixrows(8)) dotmatrix_16 (
    .row0(sram_16_bytes_16_s7), .row1(sram_16_bytes_16_s6), .row2(sram_16_bytes_16_s5),
    .row3(sram_16_bytes_16_s4), .row4(sram_16_bytes_16_s3), .row5(sram_16_bytes_16_s2),
    .row6(sram_16_bytes_16_s1), .row7(sram_16_bytes_16_s0));
endmodule

module Control_Unit_VHardwired (
  input  Enable,
  input  CLK,
  input  Reset,
  input  I4,
  input  I5,
  input  I6,
  input  I7,
  input  I2,
  input  I3,
  input  I0,
  input  I1,
  input  REG_WR_B,
  output T0,
  output T1,
  output T2,
  output T3,
  output T4,
  output T5,
  output T6,
  output T7,
  output PC_OUT,
  output MAR_IN,
  output IR,
  output PC_INC,
  output S0,
  output S1,
  output S2,
  output S3,
  output Halt,
  output PC_WR,
  output A_RD_EN,
  output B_RD_EN,
  output C_RD_EN,
  output D_RD_EN,
  output A_WR_EN,
  output B_WR_EN,
  output C_WR_EN,
  output D_WR_EN
);

  wire and_1_out, and_2_out, and_3_out, and_4_out, and_5_out, and_6_out, and_7_out, and_8_out, and_9_out,
       and_10_out, and_11_out, and_12_out, and_13_out, and_14_out, and_15_out, and_16_out, and_17_out,
       and_19_out, and_20_out, and_21_out, and_22_out, and_23_out, and_24_out, and_25_out, and_26_out,
       and_28_out, demultiplexer_1_out0, demultiplexer_1_out1, demultiplexer_1_out2, demultiplexer_1_out3,
       demultiplexer_2_out0, demultiplexer_2_out1, demultiplexer_2_out2, demultiplexer_2_out3, not_1_out,
       not_2_out, opcodedecoder_1_d0, opcodedecoder_1_d1, opcodedecoder_1_d2, opcodedecoder_1_d3,
       opcodedecoder_1_d4, opcodedecoder_1_d5, opcodedecoder_1_d6, opcodedecoder_1_d7, opcodedecoder_1_d8,
       opcodedecoder_1_d9, opcodedecoder_1_da, opcodedecoder_1_db, opcodedecoder_1_dc, opcodedecoder_1_dd,
       opcodedecoder_1_de, opcodedecoder_1_df, opcoderegister_1_o0, opcoderegister_1_o1, opcoderegister_1_o2,
       opcoderegister_1_o3, or_1_out, or_2_out, or_11_out, stepdecoder_1_s1, stepdecoder_1_s2,
       stepdecoder_1_s3, stepdecoder_1_s4, stepdecoder_1_s5, stepdecoder_1_s6, stepdecoder_1_s7,
       stepdecoder_1_s8;
  wire [1:0] cuinternaladdressreg_1_ao1, cuinternaladdressreg_1_bo1;
  wire [2:0] counter_1_q;

  not not_1 (not_1_out, Enable);
  or or_1 (or_1_out, or_11_out, and_20_out, Reset, and_24_out, and_17_out);
  Counter #(.max('h7), .width(3)) counter_1 (
    .clr(or_1_out), .up(not_1_out), .count(not_1_out), .clk(not_2_out), .Q(counter_1_q));  // open: load, D, carry
  not not_2 (not_2_out, CLK);
  CUInternalAddressReg cuinternaladdressreg_1 (
    .A_out_en(1'b1), .B_out_en(1'b1), .A1(I2), .A2(I3), .B1(I0), .B2(I1), .reset(Reset),
    .Load(stepdecoder_1_s3), .CLK(CLK), .AO1(cuinternaladdressreg_1_ao1[0]),
    .A02(cuinternaladdressreg_1_ao1[1]), .BO1(cuinternaladdressreg_1_bo1[0]),
    .BO2(cuinternaladdressreg_1_bo1[1]));  // open: A1O, A2O, B1O, B2O
  Demultiplexer #(.select(2)) demultiplexer_1 (
    .out0(demultiplexer_1_out0), .out1(demultiplexer_1_out1), .out2(demultiplexer_1_out2),
    .out3(demultiplexer_1_out3), .in(1'b1), .sel(cuinternaladdressreg_1_ao1));
  or or_2 (or_2_out, and_23_out, and_25_out, and_19_out);
  Demultiplexer #(.select(2)) demultiplexer_2 (
    .out0(demultiplexer_2_out0), .out1(demultiplexer_2_out1), .out2(demultiplexer_2_out2),
    .out3(demultiplexer_2_out3), .in(1'b1), .sel(cuinternaladdressreg_1_bo1));
  OpcodeRegister opcoderegister_1 (
    .I0(I4), .I1(I5), .I2(I6), .I3(I7), .reset(Reset), .Load(stepdecoder_1_s3), .CLK(CLK), .S0(S0), .S1(S1),
    .S2(S2), .S3(S3), .O0(opcoderegister_1_o0), .O1(opcoderegister_1_o1), .O2(opcoderegister_1_o2),
    .O3(opcoderegister_1_o3));
  and and_1 (and_1_out, PC_WR, demultiplexer_1_out0);
  and and_2 (and_2_out, PC_WR, demultiplexer_1_out1);
  and and_3 (and_3_out, PC_WR, demultiplexer_1_out2);
  and and_4 (and_4_out, demultiplexer_1_out3, PC_WR);
  and and_5 (and_5_out, or_2_out, demultiplexer_1_out0);
  and and_6 (and_6_out, or_2_out, demultiplexer_1_out1);
  and and_7 (and_7_out, or_2_out, demultiplexer_1_out2);
  and and_8 (and_8_out, or_2_out, demultiplexer_1_out3);
  and and_9 (and_9_out, demultiplexer_2_out0, and_19_out);
  and and_10 (and_10_out, demultiplexer_2_out1, and_19_out);
  and and_11 (and_11_out, demultiplexer_2_out2, and_19_out);
  and and_12 (and_12_out, demultiplexer_2_out3, and_19_out);
  and and_13 (and_13_out, demultiplexer_2_out0, REG_WR_B);
  and and_14 (and_14_out, demultiplexer_2_out1, REG_WR_B);
  and and_15 (and_15_out, demultiplexer_2_out2, REG_WR_B);
  and and_16 (and_16_out, demultiplexer_2_out3, REG_WR_B);
  or or_3 (A_WR_EN, and_5_out, and_13_out);
  or or_4 (B_WR_EN, and_6_out, and_14_out);
  or or_5 (C_WR_EN, and_7_out, and_15_out);
  or or_6 (D_WR_EN, and_8_out, and_16_out);
  OpcodeDecoder opcodedecoder_1 (
    .A4(opcoderegister_1_o3), .A3(opcoderegister_1_o2), .A2(opcoderegister_1_o1), .A1(opcoderegister_1_o0),
    .D1(opcodedecoder_1_d1), .D0(opcodedecoder_1_d0), .DF(opcodedecoder_1_df), .DE(opcodedecoder_1_de),
    .DD(opcodedecoder_1_dd), .DC(opcodedecoder_1_dc), .DB(opcodedecoder_1_db), .DA(opcodedecoder_1_da),
    .D9(opcodedecoder_1_d9), .D8(opcodedecoder_1_d8), .D7(opcodedecoder_1_d7), .D6(opcodedecoder_1_d6),
    .D5(opcodedecoder_1_d5), .D4(opcodedecoder_1_d4), .D3(opcodedecoder_1_d3), .D2(opcodedecoder_1_d2));
  or or_7 (A_RD_EN, and_9_out, and_1_out);
  or or_8 (B_RD_EN, and_10_out, and_2_out);
  or or_9 (C_RD_EN, and_11_out, and_3_out);
  or or_10 (D_RD_EN, and_12_out, and_4_out);
  StepDecoder stepdecoder_1 (
    .A2(counter_1_q[2]), .A0(counter_1_q[0]), .A1(counter_1_q[1]), .S1(stepdecoder_1_s1),
    .S2(stepdecoder_1_s2), .S3(stepdecoder_1_s3), .S4(stepdecoder_1_s4), .S5(stepdecoder_1_s5),
    .S6(stepdecoder_1_s6), .S7(stepdecoder_1_s7), .S8(stepdecoder_1_s8), .T1(T0), .T2(T1), .T3(T2), .T4(T3),
    .T5(T4), .T6(T5), .T7(T6), .T8(T7));
  and and_17 (and_17_out, opcodedecoder_1_d0, stepdecoder_1_s4);
  and and_18 (Halt, opcodedecoder_1_d1, stepdecoder_1_s4);
  and and_19 (and_19_out, opcodedecoder_1_d4, stepdecoder_1_s4);
  and and_20 (and_20_out, opcodedecoder_1_d4, stepdecoder_1_s5);
  and and_21 (and_21_out, opcodedecoder_1_d5, stepdecoder_1_s5);
  and and_22 (and_22_out, opcodedecoder_1_d5, stepdecoder_1_s4);
  and and_23 (and_23_out, opcodedecoder_1_d5, stepdecoder_1_s5);
  and and_24 (and_24_out, opcodedecoder_1_d5, stepdecoder_1_s6);
  and and_25 (and_25_out, opcodedecoder_1_dd, stepdecoder_1_s4);
  and and_26 (and_26_out, opcodedecoder_1_dd, stepdecoder_1_s5);
  and and_27 (PC_WR, opcodedecoder_1_de, stepdecoder_1_s4);
  and and_28 (and_28_out, opcodedecoder_1_de, stepdecoder_1_s5);
  or or_11 (or_11_out, and_26_out, and_28_out);
  or or_12 (PC_INC, stepdecoder_1_s3, and_21_out);
  or or_13 (MAR_IN, stepdecoder_1_s2, and_22_out);
  or or_14 (PC_OUT, and_25_out, MAR_IN);
  or or_15 (IR, and_23_out, stepdecoder_1_s3);

  // Notes on the sheet:
  //   Step Counter Reset Line
  //   Opcode Reg Load Line
  //   Address Pointer Register Enable Line
  //   Enable write Of register at address B
  //   Enable write Of register at address A
  //   Enable read Of register at address B
  //   Enable Read Of register at address A
  //   NOP
  //   HALT
  //   GETPC
  //   JMP 0xE
  //   MOV
  //   MOVI
endmodule

module OpcodeRegister (
  input  reset,
  input  Load,
  input  CLK,
  input  I0,
  input  I1,
  input  I2,
  input  I3,
  output O0,
  output O1,
  output O2,
  output O3,
  output S0,
  output S1,
  output S2,
  output S3
);

  wire and_1_out, and_2_out, and_3_out, and_4_out, and_5_out, and_6_out, and_7_out, and_8_out, buffer_1_out,
       not_1_out, or_1_out, or_2_out, or_3_out, or_4_out;

  buf buffer_1 (buffer_1_out, Load);
  not not_1 (not_1_out, Load);
  and and_1 (and_1_out, S0, not_1_out);
  and and_2 (and_2_out, buffer_1_out, I0);
  and and_3 (and_3_out, S1, not_1_out);
  and and_4 (and_4_out, buffer_1_out, I1);
  and and_5 (and_5_out, S2, not_1_out);
  and and_6 (and_6_out, buffer_1_out, I2);
  and and_7 (and_7_out, S3, not_1_out);
  and and_8 (and_8_out, buffer_1_out, I3);
  or or_1 (or_1_out, and_1_out, and_2_out);
  or or_2 (or_2_out, and_3_out, and_4_out);
  or or_3 (or_3_out, and_5_out, and_6_out);
  or or_4 (or_4_out, and_7_out, and_8_out);
  D_Flip_Flop d_ff_1 (.D(or_1_out), .clk(CLK), .Q(S0), .reset(reset));  // open: Qn, preset
  D_Flip_Flop d_ff_2 (.D(or_2_out), .clk(CLK), .Q(S1), .reset(reset));  // open: Qn, preset
  D_Flip_Flop d_ff_3 (.D(or_3_out), .clk(CLK), .Q(S2), .reset(reset));  // open: Qn, preset
  D_Flip_Flop d_ff_4 (.D(or_4_out), .clk(CLK), .Q(S3), .reset(reset));  // open: Qn, preset
  buf buffer_2 (O0, S0);
  buf buffer_3 (O1, S1);
  buf buffer_4 (O2, S2);
  buf buffer_5 (O3, S3);
endmodule

module StepDecoder (
  input  A0,
  input  A1,
  input  A2,
  output S1,
  output S2,
  output S3,
  output S4,
  output S5,
  output S6,
  output S7,
  output S8,
  output T1,
  output T2,
  output T3,
  output T4,
  output T5,
  output T6,
  output T7,
  output T8
);

  wire and_1_out, and_2_out, and_3_out, and_4_out, and_9_out, and_10_out, and_11_out, and_12_out, not_1_out,
       not_2_out, not_3_out;

  not not_1 (not_1_out, A0);
  not not_2 (not_2_out, A1);
  not not_3 (not_3_out, A2);
  and and_1 (and_1_out, not_3_out, not_2_out);
  and and_2 (and_2_out, not_3_out, not_2_out);
  and and_3 (and_3_out, not_3_out, A1);
  and and_4 (and_4_out, not_3_out, A1);
  and and_5 (S1, and_1_out, not_1_out);
  and and_6 (S2, and_2_out, A0);
  and and_7 (S3, and_3_out, not_1_out);
  and and_8 (S4, and_4_out, A0);
  and and_9 (and_9_out, A2, not_2_out);
  and and_10 (and_10_out, A2, not_2_out);
  and and_11 (and_11_out, A2, A1);
  and and_12 (and_12_out, A2, A1);
  and and_13 (S5, and_9_out, not_1_out);
  and and_14 (S6, and_10_out, A0);
  and and_15 (S7, and_11_out, not_1_out);
  and and_16 (S8, and_12_out, A0);

  assign T1 = S1;
  assign T2 = S2;
  assign T3 = S3;
  assign T4 = S4;
  assign T5 = S5;
  assign T6 = S6;
  assign T7 = S7;
  assign T8 = S8;
endmodule

module OpcodeStepCounter (
  input  Reset,
  input  EN,
  input  CLK,
  output S2,
  output S1,
  output S0
);

  wire j_k_ff_1_q, j_k_ff_2_q, j_k_ff_2_qn, j_k_ff_3_q, j_k_ff_3_qn;

  not not_1 (S2, j_k_ff_1_q);
  J_K_Flip_Flop #(.trigger("falling")) j_k_ff_1 (
    .J(EN), .K(EN), .clk(j_k_ff_2_qn), .Q(j_k_ff_1_q), .reset(Reset));  // open: Qn, preset
  not not_2 (S1, j_k_ff_2_q);
  J_K_Flip_Flop #(.trigger("falling")) j_k_ff_2 (
    .J(EN), .K(EN), .clk(j_k_ff_3_qn), .Q(j_k_ff_2_q), .Qn(j_k_ff_2_qn), .reset(Reset));  // open: preset
  not not_3 (S0, j_k_ff_3_q);
  J_K_Flip_Flop #(.trigger("falling")) j_k_ff_3 (
    .J(EN), .K(EN), .clk(CLK), .Q(j_k_ff_3_q), .Qn(j_k_ff_3_qn), .reset(Reset));  // open: preset
endmodule

module OpcodeDecoder (
  input  A4,
  input  A3,
  input  A2,
  input  A1,
  output DF,
  output DE,
  output DD,
  output DC,
  output DB,
  output DA,
  output D9,
  output D8,
  output D7,
  output D6,
  output D5,
  output D4,
  output D3,
  output D2,
  output D1,
  output D0
);

  wire and_1_out, and_2_out, and_3_out, and_4_out, and_5_out, and_6_out, and_7_out, and_8_out, and_9_out,
       and_10_out, and_11_out, and_12_out, and_13_out, and_14_out, and_15_out, and_16_out, and_25_out,
       and_26_out, and_27_out, and_28_out, and_29_out, and_30_out, and_31_out, and_32_out, and_33_out,
       and_34_out, and_35_out, and_36_out, and_37_out, and_38_out, and_39_out, and_40_out, not_1_out,
       not_2_out, not_3_out, not_4_out;

  not not_1 (not_1_out, A4);
  not not_2 (not_2_out, A3);
  not not_3 (not_3_out, A2);
  not not_4 (not_4_out, A1);
  and and_1 (and_1_out, not_1_out, not_2_out);
  and and_2 (and_2_out, not_3_out, not_4_out);
  and and_3 (and_3_out, not_1_out, not_2_out);
  and and_4 (and_4_out, not_3_out, A1);
  and and_5 (and_5_out, not_1_out, not_2_out);
  and and_6 (and_6_out, A2, not_4_out);
  and and_7 (and_7_out, not_1_out, not_2_out);
  and and_8 (and_8_out, A2, A1);
  and and_9 (and_9_out, not_1_out, A3);
  and and_10 (and_10_out, not_3_out, not_4_out);
  and and_11 (and_11_out, not_1_out, A3);
  and and_12 (and_12_out, not_3_out, A1);
  and and_13 (and_13_out, not_1_out, A3);
  and and_14 (and_14_out, A2, not_4_out);
  and and_15 (and_15_out, not_1_out, A3);
  and and_16 (and_16_out, A2, A1);
  and and_17 (D0, and_1_out, and_2_out);
  and and_18 (D1, and_3_out, and_4_out);
  and and_19 (D2, and_5_out, and_6_out);
  and and_20 (D3, and_7_out, and_8_out);
  and and_21 (D4, and_9_out, and_10_out);
  and and_22 (D5, and_11_out, and_12_out);
  and and_23 (D6, and_13_out, and_14_out);
  and and_24 (D7, and_15_out, and_16_out);
  and and_25 (and_25_out, A4, not_2_out);
  and and_26 (and_26_out, not_3_out, not_4_out);
  and and_27 (and_27_out, A4, not_2_out);
  and and_28 (and_28_out, not_3_out, A1);
  and and_29 (and_29_out, A4, not_2_out);
  and and_30 (and_30_out, A2, not_4_out);
  and and_31 (and_31_out, A4, not_2_out);
  and and_32 (and_32_out, A2, A1);
  and and_33 (and_33_out, A4, A3);
  and and_34 (and_34_out, not_3_out, not_4_out);
  and and_35 (and_35_out, A4, A3);
  and and_36 (and_36_out, not_3_out, A1);
  and and_37 (and_37_out, A4, A3);
  and and_38 (and_38_out, A2, not_4_out);
  and and_39 (and_39_out, A4, A3);
  and and_40 (and_40_out, A2, A1);
  and and_41 (D8, and_25_out, and_26_out);
  and and_42 (D9, and_27_out, and_28_out);
  and and_43 (DA, and_29_out, and_30_out);
  and and_44 (DB, and_31_out, and_32_out);
  and and_45 (DC, and_33_out, and_34_out);
  and and_46 (DD, and_35_out, and_36_out);
  and and_47 (DE, and_37_out, and_38_out);
  and and_48 (DF, and_39_out, and_40_out);

  // Notes on the sheet:
  //   easter egg!
endmodule

module CUInternalAddressReg (
  input  reset,
  input  Load,
  input  CLK,
  input  A_out_en,
  input  B_out_en,
  input  A1,
  input  A2,
  input  B1,
  input  B2,
  output AO1,
  output A02,
  output BO1,
  output BO2,
  output A1O,
  output A2O,
  output B1O,
  output B2O
);

  wire and_1_out, and_2_out, and_3_out, and_4_out, and_5_out, and_6_out, and_7_out, and_8_out, buffer_1_out,
       not_1_out, or_1_out, or_2_out, or_3_out, or_4_out;

  buf buffer_1 (buffer_1_out, Load);
  not not_1 (not_1_out, Load);
  and and_1 (and_1_out, A1O, not_1_out);
  and and_2 (and_2_out, buffer_1_out, A1);
  and and_3 (and_3_out, A2O, not_1_out);
  and and_4 (and_4_out, buffer_1_out, A2);
  and and_5 (and_5_out, B1O, not_1_out);
  and and_6 (and_6_out, buffer_1_out, B1);
  and and_7 (and_7_out, B2O, not_1_out);
  and and_8 (and_8_out, buffer_1_out, B2);
  or or_1 (or_1_out, and_1_out, and_2_out);
  or or_2 (or_2_out, and_3_out, and_4_out);
  or or_3 (or_3_out, and_5_out, and_6_out);
  or or_4 (or_4_out, and_7_out, and_8_out);
  D_Flip_Flop d_ff_1 (.D(or_1_out), .clk(CLK), .Q(A1O), .reset(reset));  // open: Qn, preset
  D_Flip_Flop d_ff_2 (.D(or_2_out), .clk(CLK), .Q(A2O), .reset(reset));  // open: Qn, preset
  D_Flip_Flop d_ff_3 (.D(or_3_out), .clk(CLK), .Q(B1O), .reset(reset));  // open: Qn, preset
  D_Flip_Flop d_ff_4 (.D(or_4_out), .clk(CLK), .Q(B2O), .reset(reset));  // open: Qn, preset
  assign AO1 = A_out_en ? A1O : 1'bz;  // Controlled_Buffer controlled_buffer_1
  assign A02 = A_out_en ? A2O : 1'bz;  // Controlled_Buffer controlled_buffer_2
  assign BO1 = B_out_en ? B1O : 1'bz;  // Controlled_Buffer controlled_buffer_3
  assign BO2 = B_out_en ? B2O : 1'bz;  // Controlled_Buffer controlled_buffer_4
endmodule

module Bit_to_7Segment (
  input  [7:0] I,
  output a1,
  output b1,
  output c1,
  output d1,
  output e1,
  output f1,
  output g1,
  output a2,
  output b2,
  output c2,
  output d2,
  output e2,
  output f2,
  output g2,
  output a3,
  output b3,
  output c3,
  output d3,
  output e3,
  output f3,
  output g3
);

  ROM #(.dataWidth(21)) rom_1 (
    .addr(I), .data({g3, f3, e3, d3, c3, b3, a3, g2, f2, e2, d2, c2, b2, a2, g1, f1, e1, d1, c1, b1, a1}));

  // Notes on the sheet:
  //   contents of rom_1 (hex, n*v repeats v):
  //   3f 6 5b 4f 66 6d 7d 7 7f 6f 33f 306 35b 34f 366 36d 37d 307 37f 36f 2dbf 2d86 2ddb 2dcf 2de6 2ded
  //   2dfd 2d87 2dff 2def 27bf 2786 27db 27cf 27e6 27ed 27fd 2787 27ff 27ef 333f 3306 335b 334f 3366 336d
  //   337d 3307 337f 336f 36bf 3686 36db 36cf 36e6 36ed 36fd 3687 36ff 36ef 3ebf 3e86 3edb 3ecf 3ee6 3eed
  //   3efd 3e87 3eff 3eef 3bf 386 3db 3cf 3e6 3ed 3fd 387 3ff 3ef 3fbf 3f86 3fdb 3fcf 3fe6 3fed 3ffd 3f87
  //   3fff 3fef 37bf 3786 37db 37cf 37e6 37ed 37fd 3787 37ff 37ef 19fbf 19f86 19fdb 19fcf 19fe6 19fed
  //   19ffd 19f87 19fff 19fef 1833f 18306 1835b 1834f 18366 1836d 1837d 18307 1837f 1836f 1adbf 1ad86
  //   1addb 1adcf 1ade6 1aded 1adfd 1ad87 1adff 1adef 1a7bf 1a786 1a7db 1a7cf 1a7e6 1a7ed 1a7fd 1a787
  //   1a7ff 1a7ef 1b33f 1b306 1b35b 1b34f 1b366 1b36d 1b37d 1b307 1b37f 1b36f 1b6bf 1b686 1b6db 1b6cf
  //   1b6e6 1b6ed 1b6fd 1b687 1b6ff 1b6ef 1bebf 1be86 1bedb 1becf 1bee6 1beed 1befd 1be87 1beff 1beef
  //   183bf 18386 183db 183cf 183e6 183ed 183fd 18387 183ff 183ef 1bfbf 1bf86 1bfdb 1bfcf 1bfe6 1bfed
  //   1bffd 1bf87 1bfff 1bfef 1b7bf 1b786 1b7db 1b7cf 1b7e6 1b7ed 1b7fd 1b787 1b7ff 1b7ef 16dfbf 16df86
  //   16dfdb 16dfcf 16dfe6 16dfed 16dffd 16df87 16dfff 16dfef 16c33f 16c306 16c35b 16c34f 16c366 16c36d
  //   16c37d 16c307 16c37f 16c36f 16edbf 16ed86 16eddb 16edcf 16ede6 16eded 16edfd 16ed87 16edff 16edef
  //   16e7bf 16e786 16e7db 16e7cf 16e7e6 16e7ed 16e7fd 16e787 16e7ff 16e7ef 16f33f 16f306 16f35b 16f34f
  //   16f366 16f36d 16f37d 16f307 16f37f 16f36f 16f6bf 16f686 16f6db 16f6cf 16f6e6 16f6ed
endmodule

module Boot_Strap_Control_Unit (
  input  CLK,
  input  [7:0] R_DATA,
  input  Enable,
  output [7:0] R_ADDR,
  output [7:0] O,
  output RAM_WR,
  output REG_RD,
  output BootStrapMode
);

  wire and_1_out, and_2_out, and_3_out, and_4_out, and_5_out, and_6_out, and_7_out, and_8_out, and_9_out,
       and_12_out, and_13_out, and_14_out, and_15_out, and_16_out, and_17_out, j_k_ff_1_q, j_k_ff_1_qn,
       or_1_out;
  wire [7:0] controlled_buffer_1_out;

  D_Flip_Flop d_ff_1 (.Qn(BootStrapMode), .preset(and_1_out), .reset(Enable));  // open: D, clk, Q
  Counter_8_bts counter_8_bts_1 (
    .PC_OUT(1'b1), .PC_INC(BootStrapMode), .CLK(j_k_ff_1_qn), .PC_RESET(Enable), .PC_WRITE(1'b0), .Q(R_ADDR));  // open: I7, I6, I5, I4, I3, I2, I1, I0, D7, D6, D5, D4, D3, D2, D1, D0
  assign controlled_buffer_1_out = j_k_ff_1_q ? R_DATA : 8'bz;  // Controlled_Buffer controlled_buffer_1
  assign controlled_buffer_1_out = j_k_ff_1_qn ? R_ADDR : 8'bz;  // Controlled_Buffer controlled_buffer_2
  J_K_Flip_Flop j_k_ff_1 (.J(CLK), .K(CLK), .clk(CLK), .Q(j_k_ff_1_q), .Qn(j_k_ff_1_qn));  // open: preset, reset
  assign O = BootStrapMode ? controlled_buffer_1_out : 8'bz;  // Controlled_Buffer controlled_buffer_3
  and and_1 (and_1_out, BootStrapMode, or_1_out);
  and and_2 (and_2_out, R_DATA[0], R_DATA[1]);
  and and_3 (and_3_out, R_DATA[2], R_DATA[3]);
  and and_4 (and_4_out, R_DATA[4], R_DATA[5]);
  and and_5 (and_5_out, R_DATA[6], R_DATA[7]);
  and and_6 (and_6_out, controlled_buffer_1_out[0], controlled_buffer_1_out[1]);
  and and_7 (and_7_out, controlled_buffer_1_out[2], controlled_buffer_1_out[3]);
  and and_8 (and_8_out, controlled_buffer_1_out[4], controlled_buffer_1_out[5]);
  and and_9 (and_9_out, controlled_buffer_1_out[6], controlled_buffer_1_out[7]);
  and and_10 (RAM_WR, j_k_ff_1_q, BootStrapMode);
  and and_11 (REG_RD, j_k_ff_1_qn, BootStrapMode);
  and and_12 (and_12_out, and_2_out, and_3_out);
  and and_13 (and_13_out, and_4_out, and_5_out);
  and and_14 (and_14_out, and_6_out, and_7_out);
  and and_15 (and_15_out, and_8_out, and_9_out);
  and and_16 (and_16_out, and_12_out, and_13_out);
  and and_17 (and_17_out, and_14_out, and_15_out);
  or or_1 (or_1_out, and_16_out, and_17_out);
endmodule

module BTLOADERTEST (
);

  wire bitregister_1_o0, bitregister_1_o1, bitregister_1_o2, bitregister_1_o3, bitregister_1_o4,
       bitregister_1_o5, bitregister_1_o6, bitregister_1_o7, button_1_out, clk_1_o,
       digital_oscilloscope_1_p2, digital_oscilloscope_1_p3, sram_256_bytes_1_s0, sram_256_bytes_1_s1,
       sram_256_bytes_1_s2, sram_256_bytes_1_s3, sram_256_bytes_1_s4, sram_256_bytes_1_s5,
       sram_256_bytes_1_s6, sram_256_bytes_1_s7;
  wire [3:0] bitregister_1_reg_out, bitregister_1_reg_out_2;
  wire [7:0] boot_strap_control_unit_1_o, boot_strap_control_unit_1_r_addr, rom_1_data;

  Button button_1 (.out(button_1_out));
  Clk clk_1 (.O(clk_1_o));  // open: halt
  // Digital_Oscilloscope digital_oscilloscope_1: pin names not known; wires that end beside it: clk_1_o, digital_oscilloscope_1_p2, digital_oscilloscope_1_p3
  Boot_Strap_Control_Unit boot_strap_control_unit_1 (
    .Enable(button_1_out), .R_DATA(rom_1_data), .CLK(clk_1_o), .RAM_WR(digital_oscilloscope_1_p3),
    .REG_RD(digital_oscilloscope_1_p2), .R_ADDR(boot_strap_control_unit_1_r_addr),
    .O(boot_strap_control_unit_1_o));  // open: BootStrapMode
  ROM rom_1 (.addr(boot_strap_control_unit_1_r_addr), .data(rom_1_data));
  Hex_Digit_Display hex_digit_display_1 (.value(bitregister_1_reg_out_2));  // open: dp
  Hex_Digit_Display hex_digit_display_2 (.value(bitregister_1_reg_out));  // open: dp
  DotMatrix #(.dotshape("circle"), .inputtype("row"), .matrixcols(1), .matrixrows(8)) dotmatrix_1 (
    .row0(bitregister_1_o0), .row1(bitregister_1_o1), .row2(bitregister_1_o2), .row3(bitregister_1_o3),
    .row4(bitregister_1_o4), .row5(bitregister_1_o5), .row6(bitregister_1_o6), .row7(bitregister_1_o7));
  BitRegister bitregister_1 (
    .Load(digital_oscilloscope_1_p2), .CLK(clk_1_o), .reg_in(boot_strap_control_unit_1_o), .reg_out_en(1'b1),
    .reg_out({bitregister_1_reg_out_2, bitregister_1_reg_out}), .O5(bitregister_1_o5), .O6(bitregister_1_o6),
    .O7(bitregister_1_o7), .O0(bitregister_1_o0), .O1(bitregister_1_o1), .O2(bitregister_1_o2),
    .O3(bitregister_1_o3), .O4(bitregister_1_o4));  // open: reset
  DotMatrix #(.dotshape("circle"), .inputtype("row"), .matrixcols(1), .matrixrows(8)) dotmatrix_2 (
    .row0(sram_256_bytes_1_s0), .row1(sram_256_bytes_1_s1), .row2(sram_256_bytes_1_s2),
    .row3(sram_256_bytes_1_s3), .row4(sram_256_bytes_1_s4), .row5(sram_256_bytes_1_s5),
    .row6(sram_256_bytes_1_s6), .row7(sram_256_bytes_1_s7));
  SRAM_256_Bytes sram_256_bytes_1 (
    .A7(bitregister_1_reg_out_2[3]), .A6(bitregister_1_reg_out_2[2]), .A5(bitregister_1_reg_out_2[1]),
    .A4(bitregister_1_reg_out_2[0]), .A3(bitregister_1_reg_out[3]), .A2(bitregister_1_reg_out[2]),
    .A1(bitregister_1_reg_out[1]), .A0(bitregister_1_reg_out[0]), .CLR(button_1_out),
    .Write(digital_oscilloscope_1_p3), .CLK(clk_1_o), .I(boot_strap_control_unit_1_o),
    .S2(sram_256_bytes_1_s2), .S3(sram_256_bytes_1_s3), .S4(sram_256_bytes_1_s4), .S5(sram_256_bytes_1_s5),
    .S6(sram_256_bytes_1_s6), .S7(sram_256_bytes_1_s7), .S0(sram_256_bytes_1_s0), .S1(sram_256_bytes_1_s1));  // open: Read, Q

  // Notes on the sheet:
  //   RAM Write Line
  //   Reg write Line
  //   contents of rom_1 (hex, n*v repeats v):
  //   2 0 4 18 f 18 2 1 4 19 f 19 3 18 9 19 7 18 4 19 12 0 10 a ff
  //   IMAR
endmodule
