// Logisim project STEPLA_1.circ as structural Verilog: 5 circuits, main circuit main
module main (
);

  wire and_1_out, bcu_1_bootstrapmode, bcu_1_ram_wr, bcu_1_reg_rd, bit_to_7segment_1_a1,
       bit_to_7segment_1_a2, bit_to_7segment_1_a3, bit_to_7segment_1_b1, bit_to_7segment_1_b2,
       bit_to_7segment_1_b3, bit_to_7segment_1_c1, bit_to_7segment_1_c2, bit_to_7segment_1_c3,
       bit_to_7segment_1_d1, bit_to_7segment_1_d2, bit_to_7segment_1_d3, bit_to_7segment_1_e1,
       bit_to_7segment_1_e2, bit_to_7segment_1_e3, bit_to_7segment_1_f1, bit_to_7segment_1_f2,
       bit_to_7segment_1_f3, bit_to_7segment_1_g1, bit_to_7segment_1_g2, bit_to_7segment_1_g3, button_1_out,
       clock_1_out, control_unit_1_accum_a_wr, control_unit_1_accum_b_wr, control_unit_1_alu_out_en,
       control_unit_1_dmar_en, control_unit_1_dram_rd, control_unit_1_dram_wr, control_unit_1_fl_en,
       control_unit_1_halt, control_unit_1_ir, control_unit_1_mar_in, control_unit_1_out_reg_wr,
       control_unit_1_pc_inc, control_unit_1_pc_out, control_unit_1_pc_wr, control_unit_1_reg_rd_en,
       control_unit_1_reg_wr_en, control_unit_1_sub, demultiplexer_1_out0, demultiplexer_1_out1,
       demultiplexer_1_out2, demultiplexer_1_out3, or_1_out, pull_resistor_2_node;
  wire [1:0] alu_1_zf, control_unit_1_dmx_in, control_unit_1_mx_in, pull_resistor_1_node,
       pull_resistor_1_node_2, register_9_q;
  wire [3:0] pull_resistor_1_node_3, register_7_q, register_7_q_2, register_10_q, register_10_q_2;
  wire [7:0] bcu_1_r_addr, counter_1_q, multiplexer_1_out, register_1_q, register_2_q, register_3_q,
       register_4_q, register_5_q, register_6_q, register_8_q, rom_1_data;

  Pull_Resistor pull_resistor_1 (.node({pull_resistor_1_node_3, pull_resistor_1_node_2, pull_resistor_1_node}));
  Demultiplexer #(.select(2)) demultiplexer_1 (
    .out0(demultiplexer_1_out0), .out1(demultiplexer_1_out1), .out2(demultiplexer_1_out2),
    .out3(demultiplexer_1_out3), .in(control_unit_1_reg_wr_en), .sel(control_unit_1_dmx_in));
  Register register_1 (
    .D({pull_resistor_1_node_3, pull_resistor_1_node_2, pull_resistor_1_node}), .en(demultiplexer_1_out0),
    .clk(and_1_out), .Q(register_1_q), .clr(button_1_out));
  Register register_2 (
    .D({pull_resistor_1_node_3, pull_resistor_1_node_2, pull_resistor_1_node}), .en(demultiplexer_1_out1),
    .clk(and_1_out), .Q(register_2_q), .clr(button_1_out));
  Control_Unit control_unit_1 (
    .Reset(button_1_out), .ZF(register_9_q[0]), .CF(register_9_q[1]), .CLK(and_1_out),
    .REG_B_ADDR(pull_resistor_1_node), .REG_A_ADDR(pull_resistor_1_node_2),
    .OPCODE_IN(pull_resistor_1_node_3), .Enable(bcu_1_bootstrapmode), .MX_IN(control_unit_1_mx_in),
    .ACCUM_A_WR(control_unit_1_accum_a_wr), .ACCUM_B_WR(control_unit_1_accum_b_wr),
    .DRAM_RD(control_unit_1_dram_rd), .DRAM_WR(control_unit_1_dram_wr), .DMAR_EN(control_unit_1_dmar_en),
    .SUB(control_unit_1_sub), .OUT_REG_WR(control_unit_1_out_reg_wr), .ALU_OUT_EN(control_unit_1_alu_out_en),
    .FL_EN(control_unit_1_fl_en), .PC_WR(control_unit_1_pc_wr), .PC_INC(control_unit_1_pc_inc),
    .Halt(control_unit_1_halt), .MAR_IN(control_unit_1_mar_in), .PC_OUT(control_unit_1_pc_out),
    .IR(control_unit_1_ir), .REG_WR_EN(control_unit_1_reg_wr_en), .REG_RD_EN(control_unit_1_reg_rd_en),
    .DMX_IN(control_unit_1_dmx_in));
  Register register_3 (
    .D({pull_resistor_1_node_3, pull_resistor_1_node_2, pull_resistor_1_node}), .en(demultiplexer_1_out2),
    .clk(and_1_out), .Q(register_3_q), .clr(button_1_out));
  Multiplexer #(.select(2), .width(8)) multiplexer_1 (
    .in0(register_1_q), .in1(register_2_q), .in2(register_3_q), .in3(register_6_q), .out(multiplexer_1_out),
    .sel(control_unit_1_mx_in));
  assign {pull_resistor_1_node_3, pull_resistor_1_node_2, pull_resistor_1_node} = control_unit_1_reg_rd_en ? multiplexer_1_out : 8'bz;  // Controlled_Buffer controlled_buffer_1
  Register register_4 (
    .D({pull_resistor_1_node_3, pull_resistor_1_node_2, pull_resistor_1_node}),
    .en(control_unit_1_accum_a_wr), .clk(and_1_out), .Q(register_4_q), .clr(button_1_out));
  Register register_5 (
    .D({pull_resistor_1_node_3, pull_resistor_1_node_2, pull_resistor_1_node}),
    .en(control_unit_1_accum_b_wr), .clk(and_1_out), .Q(register_5_q), .clr(button_1_out));
  Register register_6 (
    .D({pull_resistor_1_node_3, pull_resistor_1_node_2, pull_resistor_1_node}), .en(demultiplexer_1_out3),
    .clk(and_1_out), .Q(register_6_q), .clr(button_1_out));
  Register register_7 (
    .D({pull_resistor_1_node_3, pull_resistor_1_node_2, pull_resistor_1_node}), .en(control_unit_1_dmar_en),
    .clk(and_1_out), .Q({register_7_q_2, register_7_q}), .clr(button_1_out));
  ALU alu_1 (
    .A(register_4_q), .B(register_5_q), .SUB(control_unit_1_sub), .ALU_OUT(control_unit_1_alu_out_en),
    .CF(alu_1_zf[1]), .SIGMA({pull_resistor_1_node_3, pull_resistor_1_node_2, pull_resistor_1_node}),
    .ZF(alu_1_zf[0]));
  Hex_Digit_Display hex_digit_display_1 (.value(register_7_q_2));  // open: dp
  Hex_Digit_Display hex_digit_display_2 (.value(register_7_q));  // open: dp
  Register register_8 (
    .D({pull_resistor_1_node_3, pull_resistor_1_node_2, pull_resistor_1_node}),
    .en(control_unit_1_out_reg_wr), .clk(and_1_out), .Q(register_8_q), .clr(button_1_out));
  Register #(.width(2)) register_9 (
    .D(alu_1_zf), .en(control_unit_1_fl_en), .clk(and_1_out), .Q(register_9_q), .clr(button_1_out));
  RAM #(.asyncread("true"), .databus("bidir")) ram_1 (
    .addr({register_7_q_2, register_7_q}), .we(control_unit_1_dram_wr), .oe(control_unit_1_dram_rd),
    .clk(and_1_out), .data({pull_resistor_1_node_3, pull_resistor_1_node_2, pull_resistor_1_node}));
  _7_Segment_Display u_7_segment_display_1 (
    .g(bit_to_7segment_1_g3), .f(bit_to_7segment_1_f3), .a(bit_to_7segment_1_a3), .b(bit_to_7segment_1_b3),
    .e(bit_to_7segment_1_e3), .d(bit_to_7segment_1_d3), .c(bit_to_7segment_1_c3));  // open: dp
  _7_Segment_Display u_7_segment_display_2 (
    .g(bit_to_7segment_1_g2), .f(bit_to_7segment_1_f2), .a(bit_to_7segment_1_a2), .b(bit_to_7segment_1_b2),
    .e(bit_to_7segment_1_e2), .d(bit_to_7segment_1_d2), .c(bit_to_7segment_1_c2));  // open: dp
  _7_Segment_Display #(.decimalPoint("false")) u_7_segment_display_3 (
    .g(bit_to_7segment_1_g1), .f(bit_to_7segment_1_f1), .a(bit_to_7segment_1_a1), .b(bit_to_7segment_1_b1),
    .e(bit_to_7segment_1_e1), .d(bit_to_7segment_1_d1), .c(bit_to_7segment_1_c1));
  Bit_to_7Segment bit_to_7segment_1 (
    .I(register_8_q), .a1(bit_to_7segment_1_a1), .b1(bit_to_7segment_1_b1), .c1(bit_to_7segment_1_c1),
    .d1(bit_to_7segment_1_d1), .e1(bit_to_7segment_1_e1), .f1(bit_to_7segment_1_f1),
    .g1(bit_to_7segment_1_g1), .a2(bit_to_7segment_1_a2), .b2(bit_to_7segment_1_b2),
    .c2(bit_to_7segment_1_c2), .d2(bit_to_7segment_1_d2), .e2(bit_to_7segment_1_e2),
    .f2(bit_to_7segment_1_f2), .g2(bit_to_7segment_1_g2), .a3(bit_to_7segment_1_a3),
    .b3(bit_to_7segment_1_b3), .c3(bit_to_7segment_1_c3), .d3(bit_to_7segment_1_d3),
    .e3(bit_to_7segment_1_e3), .f3(bit_to_7segment_1_f3), .g3(bit_to_7segment_1_g3));
  Clock clock_1 (.out(clock_1_out));
  and and_1 (and_1_out, clock_1_out, ~control_unit_1_halt);  // AND_Gate
  Button button_1 (.out(button_1_out));
  Counter counter_1 (
    .clr(button_1_out), .load(control_unit_1_pc_wr), .up(control_unit_1_pc_inc),
    .count(control_unit_1_pc_inc), .clk(and_1_out),
    .D({pull_resistor_1_node_3, pull_resistor_1_node_2, pull_resistor_1_node}), .Q(counter_1_q));  // open: carry
  Pull_Resistor pull_resistor_2 (.node(pull_resistor_2_node));
  // Switch switch_1: pin names not known; wires that end beside it: button_1_out, pull_resistor_2_node
  ROM rom_1 (.addr(bcu_1_r_addr), .data(rom_1_data));
  BCU bcu_1 (
    .RESET(pull_resistor_2_node), .Enable(pull_resistor_2_node), .R_DATA(rom_1_data), .CLK(and_1_out),
    .BootStrapMode(bcu_1_bootstrapmode), .RAM_WR(bcu_1_ram_wr), .REG_RD(bcu_1_reg_rd), .R_ADDR(bcu_1_r_addr),
    .O({pull_resistor_1_node_3, pull_resistor_1_node_2, pull_resistor_1_node}));
  Multiplexer #(.width(8)) multiplexer_2 (
    .in1(counter_1_q), .out({pull_resistor_1_node_3, pull_resistor_1_node_2, pull_resistor_1_node}),
    .sel(control_unit_1_pc_out));  // open: in0
  Register register_10 (
    .D({pull_resistor_1_node_3, pull_resistor_1_node_2, pull_resistor_1_node}), .en(or_1_out),
    .clk(and_1_out), .Q({register_10_q_2, register_10_q}), .clr(button_1_out));
  or or_1 (or_1_out, control_unit_1_mar_in, bcu_1_reg_rd);
  Hex_Digit_Display hex_digit_display_3 (.value(register_10_q_2));  // open: dp
  Hex_Digit_Display hex_digit_display_4 (.value(register_10_q));  // open: dp
  RAM #(.asyncread("true"), .databus("bidir")) ram_2 (
    .addr({register_10_q_2, register_10_q}), .we(bcu_1_ram_wr), .oe(control_unit_1_ir), .clk(and_1_out),
    .data({pull_resistor_1_node_3, pull_resistor_1_node_2, pull_resistor_1_node}));

  // Notes on the sheet:
  //   contents of rom_1 (hex, n*v repeats v):
  //   50 1 54 1 5c fe 70 6c f8 a 58 2 3e b8 a 48 21 46 a0 16 80 6 fc 1 58 2 80 1e bc 1 cc 70 2e a0 1c 80
  //   1e ff
endmodule

module ALU (
  input  [7:0] A,
  input  [7:0] B,
  input  SUB,
  input  ALU_OUT,
  output ZF,
  output CF,
  output [7:0] SIGMA
);

  wire nor_1_out, nor_2_out;
  wire [7:0] adder_1_out, multiplexer_1_out, subtractor_1_out;

  Adder adder_1 (.a(A), .b(B), .out(adder_1_out), .cout(CF));  // open: cin
  Subtractor subtractor_1 (.a(A), .b(B), .out(subtractor_1_out));  // open: bin, bout
  Multiplexer #(.width(8)) multiplexer_1 (
    .in0(adder_1_out), .in1(subtractor_1_out), .out(multiplexer_1_out), .sel(SUB));
  Multiplexer #(.width(8)) multiplexer_2 (.in1(multiplexer_1_out), .out(SIGMA), .sel(ALU_OUT));  // open: in0
  nor nor_1 (nor_1_out, adder_1_out[0], adder_1_out[1], adder_1_out[2], adder_1_out[3], adder_1_out[4], adder_1_out[5], adder_1_out[6], adder_1_out[7]);
  nor nor_2 (nor_2_out, subtractor_1_out[0], subtractor_1_out[1], subtractor_1_out[2], subtractor_1_out[3], subtractor_1_out[4], subtractor_1_out[5], subtractor_1_out[6], subtractor_1_out[7]);
  or or_1 (ZF, nor_1_out, nor_2_out);
endmodule

module Bit_to_7Segment (
  input  [7:0] I,
  output a1,
  output b1,
  output c1,
  output d1,
  output e1,
  output f1,
  output g1,
  output a2,
  output b2,
  output c2,
  output d2,
  output e2,
  output f2,
  output g2,
  output a3,
  output b3,
  output c3,
  output d3,
  output e3,
  output f3,
  output g3
);

  ROM #(.dataWidth(21)) rom_1 (
    .addr(I), .data({g3, f3, e3, d3, c3, b3, a3, g2, f2, e2, d2, c2, b2, a2, g1, f1, e1, d1, c1, b1, a1}));

  // Notes on the sheet:
  //   contents of rom_1 (hex, n*v repeats v):
  //   3f 6 5b 4f 66 6d 7d 7 7f 6f 33f 306 35b 34f 366 36d 37d 307 37f 36f 2dbf 2d86 2ddb 2dcf 2de6 2ded
  //   2dfd 2d87 2dff 2def 27bf 2786 27db 27cf 27e6 27ed 27fd 2787 27ff 27ef 333f 3306 335b 334f 3366 336d
  //   337d 3307 337f 336f 36bf 3686 36db 36cf 36e6 36ed 36fd 3687 36ff 36ef 3ebf 3e86 3edb 3ecf 3ee6 3eed
  //   3efd 3e87 3eff 3eef 3bf 386 3db 3cf 3e6 3ed 3fd 387 3ff 3ef 3fbf 3f86 3fdb 3fcf 3fe6 3fed 3ffd 3f87
  //   3fff 3fef 37bf 3786 37db 37cf 37e6 37ed 37fd 3787 37ff 37ef 19fbf 19f86 19fdb 19fcf 19fe6 19fed
  //   19ffd 19f87 19fff 19fef 1833f 18306 1835b 1834f 18366 1836d 1837d 18307 1837f 1836f 1adbf 1ad86
  //   1addb 1adcf 1ade6 1aded 1adfd 1ad87 1adff 1adef 1a7bf 1a786 1a7db 1a7cf 1a7e6 1a7ed 1a7fd 1a787
  //   1a7ff 1a7ef 1b33f 1b306 1b35b 1b34f 1b366 1b36d 1b37d 1b307 1b37f 1b36f 1b6bf 1b686 1b6db 1b6cf
  //   1b6e6 1b6ed 1b6fd 1b687 1b6ff 1b6ef 1bebf 1be86 1bedb 1becf 1bee6 1beed 1befd 1be87 1beff 1beef
  //   183bf 18386 183db 183cf 183e6 183ed 183fd 18387 183ff 183ef 1bfbf 1bf86 1bfdb 1bfcf 1bfe6 1bfed
  //   1bffd 1bf87 1bfff 1bfef 1b7bf 1b786 1b7db 1b7cf 1b7e6 1b7ed 1b7fd 1b787 1b7ff 1b7ef 16dfbf 16df86
  //   16dfdb 16dfcf 16dfe6 16dfed 16dffd 16df87 16dfff 16dfef 16c33f 16c306 16c35b 16c34f 16c366 16c36d
  //   16c37d 16c307 16c37f 16c36f 16edbf 16ed86 16eddb 16edcf 16ede6 16eded 16edfd 16ed87 16edff 16edef
  //   16e7bf 16e786 16e7db 16e7cf 16e7e6 16e7ed 16e7fd 16e787 16e7ff 16e7ef 16f33f 16f306 16f35b 16f34f
  //   16f366 16f36d 16f37d 16f307 16f37f 16f36f 16f6bf 16f686 16f6db 16f6cf 16f6e6 16f6ed
endmodule

module Control_Unit (
  input  Enable,
  input  CLK,
  input  Reset,
  input  [3:0] OPCODE_IN,
  input  [1:0] REG_A_ADDR,
  input  [1:0] REG_B_ADDR,
  input  ZF,
  input  CF,
  output PC_OUT,
  output MAR_IN,
  output IR,
  output PC_INC,
  output Halt,
  output [1:0] DMX_IN,
  output [1:0] MX_IN,
  output REG_RD_EN,
  output PC_WR,
  output OUT_REG_WR,
  output REG_WR_EN,
  output ACCUM_A_WR,
  output ACCUM_B_WR,
  output ALU_OUT_EN,
  output FL_EN,
  output SUB,
  output DMAR_EN,
  output DRAM_WR,
  output DRAM_RD
);

  wire and_1_out, and_2_out, and_3_out, and_4_out, and_5_out, and_7_out, and_8_out, and_9_out, and_10_out,
       and_11_out, and_12_out, and_13_out, and_14_out, and_16_out, and_17_out, and_18_out, and_19_out,
       and_20_out, and_21_out, and_22_out, and_23_out, and_24_out, and_25_out, and_26_out, and_28_out,
       and_29_out, and_30_out, and_31_out, decoder_1_out0, decoder_1_out1, decoder_1_out2, decoder_1_out3,
       decoder_1_out4, decoder_1_out5, decoder_1_out6, decoder_1_out7, decoder_1_out8, decoder_1_out9,
       decoder_1_out10, decoder_1_out11, decoder_1_out12, decoder_1_out13, decoder_1_out14, decoder_1_out15,
       decoder_2_out0, decoder_2_out1, decoder_2_out2, decoder_2_out3, decoder_2_out4, decoder_2_out5,
       decoder_2_out6, decoder_2_out7, not_1_out, or_1_out, or_2_out, or_3_out, or_4_out, or_9_out,
       or_10_out, or_11_out, or_12_out, or_13_out, or_18_out, or_20_out, or_24_out, or_25_out, or_26_out,
       or_29_out;
  wire [1:0] multiplexer_1_out, multiplexer_2_out, multiplexer_3_out, multiplexer_4_out, register_1_q,
       register_2_q;
  wire [2:0] counter_1_q;
  wire [3:0] register_3_q;

  not not_1 (not_1_out, Enable);
  or or_1 (or_1_out, or_26_out, and_7_out, and_10_out, and_5_out);
  or or_2 (or_2_out, and_28_out, OUT_REG_WR, and_25_out, and_21_out, and_23_out, and_12_out, and_30_out);
  Counter #(.max('h7), .width(3)) counter_1 (
    .clr(Reset), .load(or_1_out), .up(not_1_out), .count(not_1_out), .clk(CLK), .D(3'b001), .Q(counter_1_q));  // open: carry
  or or_3 (or_3_out, SUB, and_10_out, and_11_out, and_24_out, and_7_out, and_18_out);
  or or_4 (or_4_out, and_22_out, and_26_out, and_29_out, and_7_out);
  Register #(.width(2)) register_1 (.D(REG_A_ADDR), .en(decoder_2_out2), .clk(CLK), .Q(register_1_q), .clr(Reset));
  Register #(.width(2)) register_2 (.D(REG_B_ADDR), .en(decoder_2_out2), .clk(CLK), .Q(register_2_q), .clr(Reset));
  Register #(.width(4)) register_3 (.D(OPCODE_IN), .en(decoder_2_out2), .clk(CLK), .Q(register_3_q), .clr(Reset));
  Multiplexer #(.width(2)) multiplexer_1 (.in0(2'b00), .in1(register_1_q), .out(multiplexer_1_out), .sel(or_3_out));
  Multiplexer #(.width(2)) multiplexer_2 (.in0(2'b00), .in1(register_2_q), .out(multiplexer_2_out), .sel(and_31_out));
  Multiplexer #(.width(2)) multiplexer_3 (.in0(2'b00), .in1(register_1_q), .out(multiplexer_3_out), .sel(or_2_out));
  or or_5 (REG_RD_EN, or_2_out, or_4_out);
  or or_6 (REG_WR_EN, or_3_out, and_31_out);
  assign DMX_IN = multiplexer_1_out | multiplexer_2_out;  // OR_Gate or_7, 2 bits wide
  assign MX_IN = multiplexer_3_out | multiplexer_4_out;  // OR_Gate or_8, 2 bits wide
  Multiplexer #(.width(2)) multiplexer_4 (.in0(2'b00), .in1(register_2_q), .out(multiplexer_4_out), .sel(or_4_out));
  Decoder #(.select(4)) decoder_1 (
    .out0(decoder_1_out0), .out1(decoder_1_out1), .out2(decoder_1_out2), .out3(decoder_1_out3),
    .out4(decoder_1_out4), .out5(decoder_1_out5), .out6(decoder_1_out6), .out7(decoder_1_out7),
    .out8(decoder_1_out8), .out9(decoder_1_out9), .out10(decoder_1_out10), .out11(decoder_1_out11),
    .out12(decoder_1_out12), .out13(decoder_1_out13), .out14(decoder_1_out14), .out15(decoder_1_out15),
    .sel(register_3_q));  // open: en
  Decoder #(.select(3)) decoder_2 (
    .out0(decoder_2_out0), .out1(decoder_2_out1), .out2(decoder_2_out2), .out3(decoder_2_out3),
    .out4(decoder_2_out4), .out5(decoder_2_out5), .out6(decoder_2_out6), .out7(decoder_2_out7),
    .sel(counter_1_q));  // open: en
  or or_9 (or_9_out, and_1_out, decoder_1_out8, and_3_out);
  or or_10 (or_10_out, and_1_out, decoder_1_out8, and_3_out);
  and and_1 (and_1_out, decoder_1_out9, ZF);
  and and_2 (and_2_out, decoder_1_out9, decoder_2_out3, ~ZF);  // AND_Gate
  and and_3 (and_3_out, decoder_1_out10, CF);
  and and_4 (and_4_out, decoder_1_out10, decoder_2_out3, ~CF);  // AND_Gate
  and and_5 (and_5_out, decoder_1_out0, decoder_2_out3);
  and and_6 (Halt, decoder_1_out1, decoder_2_out3);
  and and_7 (and_7_out, decoder_1_out4, decoder_2_out3);
  and and_8 (and_8_out, decoder_1_out5, decoder_2_out4);
  and and_9 (and_9_out, decoder_1_out5, decoder_2_out3);
  and and_10 (and_10_out, decoder_1_out5, decoder_2_out4);
  and and_11 (and_11_out, decoder_1_out13, decoder_2_out3);
  and and_12 (and_12_out, decoder_1_out14, decoder_2_out3);
  and and_13 (and_13_out, or_9_out, decoder_2_out3);
  and and_14 (and_14_out, or_10_out, decoder_2_out4);
  and and_15 (OUT_REG_WR, decoder_1_out7, decoder_2_out3);
  and and_16 (and_16_out, decoder_1_out11, decoder_2_out3);
  and and_17 (and_17_out, decoder_1_out11, decoder_2_out4);
  and and_18 (and_18_out, decoder_1_out11, decoder_2_out5);
  and and_19 (and_19_out, decoder_1_out15, decoder_2_out3);
  and and_20 (and_20_out, decoder_1_out15, decoder_2_out4);
  and and_21 (and_21_out, decoder_1_out15, decoder_2_out5);
  and and_22 (and_22_out, decoder_1_out2, decoder_2_out3);
  and and_23 (and_23_out, decoder_1_out2, decoder_2_out4);
  and and_24 (and_24_out, decoder_1_out2, decoder_2_out5);
  and and_25 (and_25_out, decoder_1_out3, decoder_2_out3);
  and and_26 (and_26_out, decoder_1_out3, decoder_2_out4);
  and and_27 (SUB, decoder_1_out3, decoder_2_out5);
  and and_28 (and_28_out, decoder_1_out6, decoder_2_out3);
  and and_29 (and_29_out, decoder_1_out6, decoder_2_out4);
  and and_30 (and_30_out, decoder_1_out12, decoder_2_out3);
  and and_31 (and_31_out, decoder_1_out12, decoder_2_out4);
  or or_11 (or_11_out, and_17_out, and_20_out);
  or or_12 (or_12_out, and_19_out, and_16_out);
  or or_13 (or_13_out, and_2_out, and_4_out);
  or or_14 (ACCUM_A_WR, and_22_out, and_25_out);
  or or_15 (ACCUM_B_WR, and_23_out, and_26_out);
  or or_16 (DMAR_EN, and_28_out, or_11_out, and_30_out);
  or or_17 (DRAM_RD, and_31_out, and_18_out);
  or or_18 (or_18_out, and_2_out, and_4_out);
  or or_19 (DRAM_WR, and_29_out, and_21_out);
  or or_20 (or_20_out, and_11_out, and_14_out, and_12_out);
  or or_21 (ALU_OUT_EN, and_24_out, SUB);
  or or_22 (PC_INC, decoder_2_out2, or_13_out, or_11_out, and_8_out);
  or or_23 (PC_WR, and_12_out, and_14_out);
  or or_24 (or_24_out, OUT_REG_WR, or_18_out, or_20_out);
  or or_25 (or_25_out, and_18_out, and_24_out, and_21_out, SUB, or_24_out);
  or or_26 (or_26_out, and_29_out, and_31_out, or_25_out);
  or or_27 (MAR_IN, and_13_out, decoder_2_out1, or_12_out, and_9_out);
  or or_28 (PC_OUT, and_11_out, MAR_IN);
  or or_29 (or_29_out, and_14_out, or_11_out);
  or or_30 (IR, and_10_out, or_29_out, decoder_2_out2);

  assign FL_EN = ALU_OUT_EN;

  // Notes on the sheet:
  //   Step Counter Reset Line
  //   Opcode Reg Load Line
  //   Address Pointer Register Enable Line
  //   Enable write Of register at address A
  //   Enable read Of register at address B
  //   Enable Write of register at address B
  //   Enable Read Of register at address A
  //   NOP
  //   JZ
  //   JC
  //   HALT
  //   GETPC
  //   JP 0xE
  //   JMP 0x8
  //   Output
  //   LDIM
  //   STIM
  //   ADD
  //   SUB
  //   STRD
  //   MOV
  //   MOVI
  //   LDD
  //   Reset line
  //   Reset
endmodule

module BCU (
  input  RESET,
  input  CLK,
  input  [7:0] R_DATA,
  input  Enable,
  output [7:0] R_ADDR,
  output [7:0] O,
  output RAM_WR,
  output REG_RD,
  output BootStrapMode
);

  wire and_1_out, and_2_out, and_3_out, and_4_out, and_5_out, and_6_out, and_7_out, and_8_out, and_9_out,
       and_12_out, and_13_out, and_14_out, and_15_out, and_16_out, and_17_out, j_k_ff_1_q, j_k_ff_1_qn,
       or_1_out;
  wire [7:0] controlled_buffer_1_out;

  Counter counter_1 (
    .clr(RESET), .up(BootStrapMode), .count(BootStrapMode), .clk(j_k_ff_1_qn), .Q(R_ADDR));  // open: load, D, carry
  D_Flip_Flop d_ff_1 (.Qn(BootStrapMode), .preset(and_1_out), .reset(Enable));  // open: D, clk, Q
  assign controlled_buffer_1_out = j_k_ff_1_q ? R_DATA : 8'bz;  // Controlled_Buffer controlled_buffer_1
  assign controlled_buffer_1_out = j_k_ff_1_qn ? R_ADDR : 8'bz;  // Controlled_Buffer controlled_buffer_2
  J_K_Flip_Flop j_k_ff_1 (
    .J(CLK), .K(CLK), .clk(CLK), .Q(j_k_ff_1_q), .Qn(j_k_ff_1_qn), .reset(Enable));  // open: preset
  assign O = BootStrapMode ? controlled_buffer_1_out : 8'bz;  // Controlled_Buffer controlled_buffer_3
  and and_1 (and_1_out, BootStrapMode, or_1_out);
  and and_2 (and_2_out, R_DATA[0], R_DATA[1]);
  and and_3 (and_3_out, R_DATA[2], R_DATA[3]);
  and and_4 (and_4_out, R_DATA[4], R_DATA[5]);
  and and_5 (and_5_out, R_DATA[6], R_DATA[7]);
  and and_6 (and_6_out, controlled_buffer_1_out[0], controlled_buffer_1_out[1]);
  and and_7 (and_7_out, controlled_buffer_1_out[2], controlled_buffer_1_out[3]);
  and and_8 (and_8_out, controlled_buffer_1_out[4], controlled_buffer_1_out[5]);
  and and_9 (and_9_out, controlled_buffer_1_out[6], controlled_buffer_1_out[7]);
  and and_10 (RAM_WR, j_k_ff_1_q, BootStrapMode);
  and and_11 (REG_RD, j_k_ff_1_qn, BootStrapMode);
  and and_12 (and_12_out, and_2_out, and_3_out);
  and and_13 (and_13_out, and_4_out, and_5_out);
  and and_14 (and_14_out, and_6_out, and_7_out);
  and and_15 (and_15_out, and_8_out, and_9_out);
  and and_16 (and_16_out, and_12_out, and_13_out);
  and and_17 (and_17_out, and_14_out, and_15_out);
  or or_1 (or_1_out, and_16_out, and_17_out);
endmodule
